// Logisim project 7 Procesador 16 bits II.circ as structural Verilog: 26 circuits, main circuit main
module main (
);

  wire alu_1_bbit, clock_1_out, d_ff_1_q, jmp_1_cls, jmp_1_jact, keyboard_1_avail, mem_1_actr,
       multiplexer_1_out, not_1_out, not_2_out, not_3_out, not_4_out, reg_s_1_b7, reg_s_1_b8, Reset_2_out,
       Reset_out;
  wire [3:0] binario_a_decimal_16_bits_1_out_2, binario_a_decimal_16_bits_1_out_3,
       binario_a_decimal_16_bits_1_out_4, binario_a_decimal_16_bits_1_out_5,
       binario_a_decimal_16_bits_1_out_6, rom_1_data, rom_1_data_2, rom_1_data_3, rom_1_data_4;
  wire [6:0] keyboard_1_data, reg_s_1_salida;
  wire [15:0] counter_1_q, jmp_1_imm, jmp_1_pcdata, mem_1_address_rf1, mem_1_store_rf2, ram_1_data,
       reg_s_1_rsrc1, reg_s_1_rsrc2;

  not not_1 (not_1_out, jmp_1_jact);
  Counter #(.width(16), .max('hffff)) counter_1 (
    .load(jmp_1_jact), .D(jmp_1_imm), .count(not_1_out), .Q(counter_1_q), .clk(clock_1_out), .clr(Reset_out));  // open: carry
  JMP jmp_1 (
    .NEM(rom_1_data_4), .RF2(rom_1_data), .RF1(rom_1_data_2), .RD(rom_1_data_3), .RF1_2(reg_s_1_rsrc1),
    .Imm(jmp_1_imm), .Jact(jmp_1_jact), .PCdata(jmp_1_pcdata), .CLS(jmp_1_cls), .PC(counter_1_q),
    .Bbit(multiplexer_1_out));
  Button Reset (.out(Reset_out));
  MEM mem_1 (
    .NEM(rom_1_data_4), .RF1(rom_1_data_2), .RF2(rom_1_data), .RD(rom_1_data_3),
    .Direccion_RF1(reg_s_1_rsrc1), .Guardar_RF2(reg_s_1_rsrc2), .Redest_RD(ram_1_data),
    .Resultados(jmp_1_pcdata), .Address_RF1(mem_1_address_rf1), .Store_RF2(mem_1_store_rf2), .actR(mem_1_actr));
  Hex_Digit_Display hex_digit_display_1 (.value(binario_a_decimal_16_bits_1_out_2));  // open: dp
  Binario_a_decimal_16_bits binario_a_decimal_16_bits_1 (
    .in_1(ram_1_data), .out_2(binario_a_decimal_16_bits_1_out_2), .out_3(binario_a_decimal_16_bits_1_out_3),
    .out_4(binario_a_decimal_16_bits_1_out_4), .out_5(binario_a_decimal_16_bits_1_out_5),
    .out_6(binario_a_decimal_16_bits_1_out_6));
  Hex_Digit_Display hex_digit_display_2 (.value(rom_1_data_3));  // open: dp
  Hex_Digit_Display hex_digit_display_3 (.value(rom_1_data_4));  // open: dp
  Clock clock_1 (.out(clock_1_out));
  Hex_Digit_Display hex_digit_display_4 (.value(binario_a_decimal_16_bits_1_out_3));  // open: dp
  Hex_Digit_Display hex_digit_display_5 (.value(binario_a_decimal_16_bits_1_out_4));  // open: dp
  ROM #(.addrWidth(16), .dataWidth(16)) rom_1 (
    .addr(counter_1_q), .data({rom_1_data_4, rom_1_data_3, rom_1_data_2, rom_1_data}));  // open: sel
  Hex_Digit_Display hex_digit_display_6 (.value(rom_1_data));  // open: dp
  Hex_Digit_Display hex_digit_display_7 (.value(rom_1_data_2));  // open: dp
  Hex_Digit_Display hex_digit_display_8 (.value(binario_a_decimal_16_bits_1_out_6));  // open: dp
  Hex_Digit_Display hex_digit_display_9 (.value(binario_a_decimal_16_bits_1_out_5));  // open: dp
  LED led_1 (.in(reg_s_1_b8));
  not not_2 (not_2_out, mem_1_actr);
  ALU alu_1 (
    .NEM(rom_1_data_4), .RD(rom_1_data_3), .RS2(reg_s_1_rsrc2), .RS1(reg_s_1_rsrc1), .Bbit(alu_1_bbit),
    .Result(jmp_1_pcdata));
  D_Flip_Flop d_ff_1 (.clk(clock_1_out), .D(alu_1_bbit), .Q(d_ff_1_q));  // open: Qn, preset, en, reset
  Keyboard keyboard_1 (
    .clk(clock_1_out), .re(reg_s_1_b8), .clr(not_3_out), .avail(keyboard_1_avail), .data(keyboard_1_data));
  not not_3 (not_3_out, reg_s_1_b8);
  RAM #(.addrWidth(16), .dataWidth(16), .bus("separate")) ram_1 (
    .addr(mem_1_address_rf1), .din(mem_1_store_rf2), .data(ram_1_data), .str(mem_1_actr), .clk(clock_1_out),
    .ld(not_2_out), .clr(Reset_2_out));  // open: sel
  Multiplexer #(.enable("false")) multiplexer_1 (
    .in0(d_ff_1_q), .in1(not_4_out), .out(multiplexer_1_out), .sel(reg_s_1_b8));
  Button Reset_2 (.out(Reset_2_out));
  REG_S reg_s_1 (
    .Bbit(multiplexer_1_out), .CLOCK(clock_1_out), .RD(rom_1_data_3), .Rsrc2(reg_s_1_rsrc2),
    .Rsrc1(reg_s_1_rsrc1), .RF1(rom_1_data_2), .RF2(rom_1_data), .NEM(rom_1_data_4), .DataR(jmp_1_pcdata),
    .ASCII(keyboard_1_data), .Salida(reg_s_1_salida), .B8(reg_s_1_b8), .B7(reg_s_1_b7));
  not not_4 (not_4_out, keyboard_1_avail);
  TTY #(.rows(35), .cols(72)) tty_1 (.data(reg_s_1_salida), .clk(clock_1_out), .we(reg_s_1_b7), .clr(jmp_1_cls));

  // Notes on the sheet:
  //   contents of rom_1 (hex, n*v repeats v):
  //   a200 fe00 c050 fe00 c07a f100 a216 b201 fe00 c050 fe00 c02f a2a1 b203 224 9220 e020 c010 29*0 aa00
  //   a101 a202 a380 a600 a77f a90a b001 7000 d038 7009 d040 3003 2007 1661 8060 c036 a301 a400 ab30 9860
  //   661 1c8b 5c3 445 339 706a d04c c043 a202 ee2 e0e0 0 aa00 ab01 9020 700a d04c a380 3003 a000 22b c052
  //   6*0 a600 aa0a a330 a101 a400 1661 8064 175a 255a 853 1661 8068 7074 d070 8157 c067 8126 81fe f0e0
  //   c050 81ef c04c 4*0 b001 7000 d07c c04c 130*0 a249 b202 fe00 c050 a20b b202 fe00 c050 fe00 c02f 81d4
  //   a223 b202 fe00 c050 fe00 c02f cd4 a23c b202 fe00 c050 815c fe00 c060 fe00 c07a c005 4*0 a25b b202
  //   fe00 c050 a20b b202 fe00 c050 fe00 c030 81d4 a223 b202 fe00 c050 fe00 c030 dd4 a23c b202 fe00 c050
  //   815d fe00 c060 fe00 c07a c005 4*0 a26e b202 fe00 c050 a20b b202 fe00 c050 fe00 c02f 81d4 a223 b202
  //   fe00 c050 fe00 c02f 1cd4 a23c b202 fe00 c050 815c fe00 c060 fe00 c07a c005 4*0 a282 b202 fe00 c050
  //   a20b b202 fe00 c050 fe00 c030 81d4 a223 b202 fe00 c050 fe00 c030 1dd4 a23c b202 fe00 c050 815d fe00
  //   c060 fe00 c07a c005 4*0 a295 b202 fe00 c050 a20b b202 fe00 c050 fe00 c02f 81d4 a223 b202 fe00 c050
  //   fe00 c030 2dd4 a23c b202 fe00 c050 815d fe00 c060 fe00 c07a c005 4*0 a2a9 b202 fe00 c050 a20b b202
  //   fe00 c050 fe00 c02f 81d4 a223 b202 fe00 c050 fe00 c030 2cd4 a23c b202 fe00 c050 815c fe00 c060 fe00
  //   c07a c005 4*0 a2bd b202 fe00 c050 a20b b202 fe00 c050 fe00 c02f 81d4 a223 b202 fe00 c050 fe00 c030
  //   3c40 a23c b202 fe00 c050 815c fe00 c060 fe00 c07a c005 4*0 a2d2 b202 fe00 c050 a20b b202 fe00 c050
  //   fe00 c02f 81d4 a223 b202 fe00 c050 fe00 c030 3d40 a23c b202 fe00 c050 815d fe00 c060 fe00 c07a c005
  //   4*0 a2e6 b202 fe00 c050 a20b b202 fe00 c050 fe00 c02f 4c40 a23c b202 fe00 c050 815c fe00 c060 fe00
  //   c07a c005 11*0 a212 b203 fe00 c050 a20b b202 fe00 c050 fe00 c02f 5c40 a23c b202 fe00 c050 815c fe00
  //   c060 fe00 c07a c005 11*0 a2fc b202 fe00 c050 a20b b202 fe00 c050 fe00 c030 4d40 a23c b202 fe00 c050
  //   815c fe00 c060 fe00 c07a c005 11*0 a228 b203 fe00 c050 a20b b202 fe00 c050 fe00 c02f 5d40 a23c b202
  //   fe00 c050 815c fe00 c060 fe00 c07a c005 11*0 a23e b203 fe00 c050 a20b b202 fe00 c050 fe00 c02f 81d4
  //   a223 b202 fe00 c050 fe00 c02f ac01 60d4 d295 ac00 a23c b202 fe00 c050 815c fe00 c060 fe00 c07a c005
  //   0 a258 b203 fe00 c050 a20b b202 fe00 c050 fe00 c02f 81d4 a223 b202 fe00 c050 fe00 c02f ac01 61d4
  //   d2b5 ac00 a23c b202 fe00 c050 815c fe00 c060 fe00 c07a c005 0 a272 b203 fe00 c050 a20b b202 fe00
  //   c050 fe00 c02f 81d4 a223 b202 fe00 c050 fe00 c02f ac01 70d4 d2d5 ac00 a23c b202 fe00 c050 815c fe00
  //   c060 fe00 c07a c005 0 a28a b203 fe00 c050 a20b b202 fe00 c050 fe00 c02f 81d4 a223 b202 fe00 c050
  //   fe00 c02f ac01 71d4 d2f5 ac00 a23c b202 fe00 c050 815c fe00 c060 fe00 c07a c005
  //   Procesador 16 bits
  //   Datos del estudiante
  //   Abdiel Mendoza
  //   3-749-1302
  //   1LS-132
  //   TECLADO
endmodule

module ADD (
  input  [15:0] A,
  input  [15:0] B,
  output [15:0] Result,
  output out_4
);

  wire and_1_out, and_2_out, and_3_out, and_4_out, and_5_out, and_6_out, and_7_out, and_8_out, and_9_out,
       and_10_out, and_11_out, and_12_out, and_13_out, and_14_out, and_15_out, and_16_out, and_17_out,
       and_18_out, and_19_out, and_20_out, and_21_out, and_22_out, and_23_out, and_24_out, and_25_out,
       and_26_out, and_27_out, and_28_out, and_29_out, and_30_out, and_31_out, and_32_out, C_2_out, C_3_out,
       C_4_out, C_5_out, C_6_out, C_7_out, C_8_out, C_9_out, C_10_out, C_11_out, C_12_out, C_13_out,
       C_15_out, C_16_out, C_out, xor_1_out, xor_2_out, xor_3_out, xor_4_out, xor_5_out, xor_6_out,
       xor_7_out, xor_8_out, xor_9_out, xor_10_out, xor_11_out, xor_12_out, xor_13_out, xor_14_out,
       xor_15_out, xor_16_out;

  and and_1 (and_1_out, A[0], B[0]);
  and and_2 (and_2_out, A[1], B[1]);
  and and_3 (and_3_out, A[2], B[2]);
  and and_4 (and_4_out, A[4], B[4]);
  and and_5 (and_5_out, A[5], B[5]);
  and and_6 (and_6_out, A[7], B[7]);
  and and_7 (and_7_out, A[8], B[8]);
  and and_8 (and_8_out, A[9], B[9]);
  and and_9 (and_9_out, A[10], B[10]);
  and and_10 (and_10_out, A[11], B[11]);
  and and_11 (and_11_out, A[12], B[12]);
  and and_12 (and_12_out, A[13], B[13]);
  and and_13 (and_13_out, A[14], B[14]);
  and and_14 (and_14_out, A[15], B[15]);
  xor xor_1 (xor_1_out, A[0], B[0]);
  xor xor_2 (xor_2_out, A[1], B[1]);
  xor xor_3 (xor_3_out, A[2], B[2]);
  xor xor_4 (xor_4_out, A[3], B[3]);
  and and_15 (and_15_out, A[3], B[3]);
  xor xor_5 (xor_5_out, A[4], B[4]);
  xor xor_6 (xor_6_out, A[5], B[5]);
  xor xor_7 (xor_7_out, A[6], B[6]);
  and and_16 (and_16_out, A[6], B[6]);
  xor xor_8 (xor_8_out, A[7], B[7]);
  xor xor_9 (xor_9_out, A[8], B[8]);
  xor xor_10 (xor_10_out, A[9], B[9]);
  xor xor_11 (xor_11_out, A[10], B[10]);
  xor xor_12 (xor_12_out, A[11], B[11]);
  xor xor_13 (xor_13_out, A[12], B[12]);
  xor xor_14 (xor_14_out, A[13], B[13]);
  xor xor_15 (xor_15_out, A[14], B[14]);
  xor xor_16 (xor_16_out, A[15], B[15]);
  xor xor_17 (Result[0], xor_1_out, 1'b0);
  or C (C_out, and_17_out, and_1_out);
  and and_17 (and_17_out, xor_1_out, 1'b0);
  xor xor_18 (Result[1], xor_2_out, C_out);
  or C_2 (C_2_out, and_18_out, and_2_out);
  and and_18 (and_18_out, xor_2_out, C_out);
  xor xor_19 (Result[2], xor_3_out, C_2_out);
  and and_19 (and_19_out, xor_3_out, C_2_out);
  or C_3 (C_3_out, and_19_out, and_3_out);
  xor xor_20 (Result[3], xor_4_out, C_3_out);
  and and_20 (and_20_out, xor_4_out, C_3_out);
  xor xor_21 (Result[4], xor_5_out, C_15_out);
  or C_4 (C_4_out, and_21_out, and_4_out);
  and and_21 (and_21_out, xor_5_out, C_15_out);
  xor xor_22 (Result[5], xor_6_out, C_4_out);
  and and_22 (and_22_out, xor_6_out, C_4_out);
  or C_5 (C_5_out, and_22_out, and_5_out);
  xor xor_23 (Result[6], xor_7_out, C_5_out);
  and and_23 (and_23_out, xor_7_out, C_5_out);
  xor xor_24 (Result[7], xor_8_out, C_16_out);
  or C_6 (C_6_out, and_24_out, and_6_out);
  and and_24 (and_24_out, xor_8_out, C_16_out);
  xor xor_25 (Result[8], xor_9_out, C_6_out);
  or C_7 (C_7_out, and_25_out, and_7_out);
  and and_25 (and_25_out, xor_9_out, C_6_out);
  xor xor_26 (Result[9], xor_10_out, C_7_out);
  and and_26 (and_26_out, xor_10_out, C_7_out);
  or C_8 (C_8_out, and_26_out, and_8_out);
  xor xor_27 (Result[10], xor_11_out, C_8_out);
  and and_27 (and_27_out, xor_11_out, C_8_out);
  or C_9 (C_9_out, and_27_out, and_9_out);
  xor xor_28 (Result[11], xor_12_out, C_9_out);
  or C_10 (C_10_out, and_28_out, and_10_out);
  and and_28 (and_28_out, xor_12_out, C_9_out);
  xor xor_29 (Result[12], xor_13_out, C_10_out);
  and and_29 (and_29_out, xor_13_out, C_10_out);
  or C_11 (C_11_out, and_29_out, and_11_out);
  xor xor_30 (Result[13], xor_14_out, C_11_out);
  and and_30 (and_30_out, xor_14_out, C_11_out);
  or C_12 (C_12_out, and_30_out, and_12_out);
  xor xor_31 (Result[14], xor_15_out, C_12_out);
  or C_13 (C_13_out, and_31_out, and_13_out);
  and and_31 (and_31_out, xor_15_out, C_12_out);
  xor xor_32 (Result[15], xor_16_out, C_13_out);
  and and_32 (and_32_out, xor_16_out, C_13_out);
  or C_14 (out_4, and_32_out, and_14_out);
  or C_15 (C_15_out, and_20_out, and_15_out);
  or C_16 (C_16_out, and_23_out, and_16_out);
endmodule

module SUB (
  input  [15:0] M,
  input  [15:0] S,
  output [15:0] out_3,
  output Borrow
);

  wire and_1_out, and_2_out, and_3_out, and_4_out, and_5_out, and_6_out, and_7_out, and_8_out, and_9_out,
       and_10_out, and_11_out, and_12_out, and_13_out, and_14_out, and_15_out, and_16_out, and_17_out,
       and_18_out, and_19_out, and_20_out, and_21_out, and_22_out, and_23_out, and_24_out, and_25_out,
       and_26_out, and_27_out, and_28_out, and_29_out, and_30_out, and_31_out, and_32_out, B_2_out, B_3_out,
       B_4_out, B_5_out, B_6_out, B_7_out, B_8_out, B_9_out, B_10_out, B_11_out, B_12_out, B_13_out,
       B_14_out, B_15_out, B_out, not_1_out, not_2_out, not_3_out, not_4_out, not_5_out, not_6_out,
       not_7_out, not_8_out, not_9_out, not_10_out, not_11_out, not_12_out, not_13_out, not_14_out,
       not_15_out, not_16_out, not_17_out, not_18_out, not_19_out, not_20_out, not_21_out, not_22_out,
       not_23_out, not_24_out, not_25_out, not_26_out, not_27_out, not_28_out, not_29_out, not_30_out,
       not_31_out, not_32_out, xor_1_out, xor_2_out, xor_3_out, xor_4_out, xor_5_out, xor_6_out, xor_7_out,
       xor_8_out, xor_9_out, xor_10_out, xor_11_out, xor_12_out, xor_13_out, xor_14_out, xor_15_out,
       xor_16_out;

  not not_1 (not_1_out, M[12]);
  not not_2 (not_2_out, M[13]);
  not not_3 (not_3_out, M[14]);
  not not_4 (not_4_out, M[15]);
  not not_5 (not_5_out, M[4]);
  not not_6 (not_6_out, M[5]);
  not not_7 (not_7_out, M[6]);
  not not_8 (not_8_out, M[7]);
  not not_9 (not_9_out, M[8]);
  not not_10 (not_10_out, M[9]);
  not not_11 (not_11_out, M[10]);
  not not_12 (not_12_out, M[11]);
  not not_13 (not_13_out, M[0]);
  not not_14 (not_14_out, M[1]);
  not not_15 (not_15_out, M[2]);
  not not_16 (not_16_out, M[3]);
  xor xor_1 (xor_1_out, M[0], S[0]);
  and and_1 (and_1_out, not_13_out, S[0]);
  xor xor_2 (xor_2_out, M[1], S[1]);
  and and_2 (and_2_out, not_14_out, S[1]);
  xor xor_3 (xor_3_out, M[2], S[2]);
  and and_3 (and_3_out, not_15_out, S[2]);
  xor xor_4 (xor_4_out, M[3], S[3]);
  and and_4 (and_4_out, not_16_out, S[3]);
  xor xor_5 (xor_5_out, M[4], S[4]);
  and and_5 (and_5_out, not_5_out, S[4]);
  xor xor_6 (xor_6_out, M[5], S[5]);
  and and_6 (and_6_out, not_6_out, S[5]);
  xor xor_7 (xor_7_out, M[6], S[6]);
  and and_7 (and_7_out, not_7_out, S[6]);
  xor xor_8 (xor_8_out, M[7], S[7]);
  and and_8 (and_8_out, not_8_out, S[7]);
  xor xor_9 (xor_9_out, M[8], S[8]);
  and and_9 (and_9_out, not_9_out, S[8]);
  xor xor_10 (xor_10_out, M[9], S[9]);
  and and_10 (and_10_out, not_10_out, S[9]);
  xor xor_11 (xor_11_out, M[10], S[10]);
  and and_11 (and_11_out, not_11_out, S[10]);
  xor xor_12 (xor_12_out, M[11], S[11]);
  and and_12 (and_12_out, not_12_out, S[11]);
  xor xor_13 (xor_13_out, M[12], S[12]);
  and and_13 (and_13_out, not_1_out, S[12]);
  xor xor_14 (xor_14_out, M[13], S[13]);
  and and_14 (and_14_out, not_2_out, S[13]);
  xor xor_15 (xor_15_out, M[14], S[14]);
  and and_15 (and_15_out, not_3_out, S[14]);
  xor xor_16 (xor_16_out, M[15], S[15]);
  and and_16 (and_16_out, not_4_out, S[15]);
  xor T (out_3[0], xor_1_out, 1'b0);
  not not_17 (not_17_out, xor_1_out);
  and and_17 (and_17_out, not_17_out, 1'b0);
  xor xor_17 (out_3[1], xor_2_out, B_out);
  not not_18 (not_18_out, xor_2_out);
  and and_18 (and_18_out, not_18_out, B_out);
  xor xor_18 (out_3[2], xor_3_out, B_2_out);
  not not_19 (not_19_out, xor_3_out);
  and and_19 (and_19_out, not_19_out, B_2_out);
  xor xor_19 (out_3[3], xor_4_out, B_3_out);
  not not_20 (not_20_out, xor_4_out);
  and and_20 (and_20_out, not_20_out, B_3_out);
  xor xor_20 (out_3[4], xor_5_out, B_4_out);
  not not_21 (not_21_out, xor_5_out);
  and and_21 (and_21_out, not_21_out, B_4_out);
  xor xor_21 (out_3[5], xor_6_out, B_5_out);
  not not_22 (not_22_out, xor_6_out);
  and and_22 (and_22_out, not_22_out, B_5_out);
  xor xor_22 (out_3[6], xor_7_out, B_6_out);
  not not_23 (not_23_out, xor_7_out);
  and and_23 (and_23_out, not_23_out, B_6_out);
  xor xor_23 (out_3[7], xor_8_out, B_7_out);
  not not_24 (not_24_out, xor_8_out);
  and and_24 (and_24_out, not_24_out, B_7_out);
  xor xor_24 (out_3[8], xor_9_out, B_8_out);
  not not_25 (not_25_out, xor_9_out);
  and and_25 (and_25_out, not_25_out, B_8_out);
  xor xor_25 (out_3[9], xor_10_out, B_9_out);
  not not_26 (not_26_out, xor_10_out);
  and and_26 (and_26_out, not_26_out, B_9_out);
  xor xor_26 (out_3[10], xor_11_out, B_10_out);
  not not_27 (not_27_out, xor_11_out);
  and and_27 (and_27_out, not_27_out, B_10_out);
  xor xor_27 (out_3[11], xor_12_out, B_11_out);
  not not_28 (not_28_out, xor_12_out);
  and and_28 (and_28_out, not_28_out, B_11_out);
  xor xor_28 (out_3[12], xor_13_out, B_12_out);
  not not_29 (not_29_out, xor_13_out);
  and and_29 (and_29_out, not_29_out, B_12_out);
  xor xor_29 (out_3[13], xor_14_out, B_13_out);
  not not_30 (not_30_out, xor_14_out);
  and and_30 (and_30_out, not_30_out, B_13_out);
  xor xor_30 (out_3[14], xor_15_out, B_14_out);
  not not_31 (not_31_out, xor_15_out);
  and and_31 (and_31_out, not_31_out, B_14_out);
  xor xor_31 (out_3[15], xor_16_out, B_15_out);
  not not_32 (not_32_out, xor_16_out);
  and and_32 (and_32_out, not_32_out, B_15_out);
  or B (B_out, and_17_out, and_1_out);
  or B_2 (B_2_out, and_18_out, and_2_out);
  or B_3 (B_3_out, and_19_out, and_3_out);
  or B_4 (B_4_out, and_20_out, and_4_out);
  or B_5 (B_5_out, and_21_out, and_5_out);
  or B_6 (B_6_out, and_22_out, and_6_out);
  or B_7 (B_7_out, and_7_out, and_23_out);
  or B_8 (B_8_out, and_8_out, and_24_out);
  or B_9 (B_9_out, and_9_out, and_25_out);
  or B_10 (B_10_out, and_10_out, and_26_out);
  or B_11 (B_11_out, and_11_out, and_27_out);
  or B_12 (B_12_out, and_12_out, and_28_out);
  or B_13 (B_13_out, and_13_out, and_29_out);
  or B_14 (B_14_out, and_14_out, and_30_out);
  or B_15 (B_15_out, and_15_out, and_31_out);
  or B_16 (Borrow, and_16_out, and_32_out);
endmodule

module AND (
  input  [15:0] R1,
  input  [15:0] R2,
  output [15:0] Re
);

  and and_1 (Re[0], R1[0], R2[0]);
  and and_2 (Re[1], R1[1], R2[1]);
  and and_3 (Re[2], R1[2], R2[2]);
  and and_4 (Re[3], R1[3], R2[3]);
  and and_5 (Re[4], R1[4], R2[4]);
  and and_6 (Re[5], R1[5], R2[5]);
  and and_7 (Re[6], R1[6], R2[6]);
  and and_8 (Re[7], R1[7], R2[7]);
  and and_9 (Re[8], R1[8], R2[8]);
  and and_10 (Re[9], R1[9], R2[9]);
  and and_11 (Re[10], R1[10], R2[10]);
  and and_12 (Re[11], R1[11], R2[11]);
  and and_13 (Re[12], R1[12], R2[12]);
  and and_14 (Re[13], R1[13], R2[13]);
  and and_15 (Re[14], R1[14], R2[14]);
  and and_16 (Re[15], R1[15], R2[15]);
endmodule

module OR (
  input  [15:0] R1,
  input  [15:0] R2,
  output [15:0] Re
);

  or or_1 (Re[0], R1[0], R2[0]);
  or or_2 (Re[1], R1[1], R2[1]);
  or or_3 (Re[2], R1[2], R2[2]);
  or or_4 (Re[3], R1[3], R2[3]);
  or or_5 (Re[4], R1[4], R2[4]);
  or or_6 (Re[5], R1[5], R2[5]);
  or or_7 (Re[6], R1[6], R2[6]);
  or or_8 (Re[7], R1[7], R2[7]);
  or or_9 (Re[8], R1[8], R2[8]);
  or or_10 (Re[9], R1[9], R2[9]);
  or or_11 (Re[10], R1[10], R2[10]);
  or or_12 (Re[11], R1[11], R2[11]);
  or or_13 (Re[12], R1[12], R2[12]);
  or or_14 (Re[13], R1[13], R2[13]);
  or or_15 (Re[14], R1[14], R2[14]);
  or or_16 (Re[15], R1[15], R2[15]);
endmodule

module XOR (
  input  [15:0] in_1,
  input  [15:0] in_2,
  output [15:0] Resp
);

  xor xor_1 (Resp[0], in_1[0], in_2[0]);
  xor xor_2 (Resp[1], in_1[1], in_2[1]);
  xor xor_3 (Resp[2], in_1[2], in_2[2]);
  xor xor_4 (Resp[3], in_1[3], in_2[3]);
  xor xor_5 (Resp[4], in_1[4], in_2[4]);
  xor xor_6 (Resp[5], in_1[5], in_2[5]);
  xor xor_7 (Resp[6], in_1[6], in_2[6]);
  xor xor_8 (Resp[7], in_1[7], in_2[7]);
  xor xor_9 (Resp[8], in_1[8], in_2[8]);
  xor xor_10 (Resp[9], in_1[9], in_2[9]);
  xor xor_11 (Resp[10], in_1[10], in_2[10]);
  xor xor_12 (Resp[11], in_1[11], in_2[11]);
  xor xor_13 (Resp[12], in_1[12], in_2[12]);
  xor xor_14 (Resp[13], in_1[13], in_2[13]);
  xor xor_15 (Resp[14], in_1[14], in_2[14]);
  xor xor_16 (Resp[15], in_1[15], in_2[15]);

  // Notes on the sheet:
  //   R1
  //   R2
  //   CIRCUITO XOR
endmodule

module SR (
  input  [15:0] N1,
  output Overflow,
  output [15:0] Result
);


  assign Overflow = N1[0];
  assign Result = {1'b0, N1[15:1]};
endmodule

module RR (
  input  [15:0] N1,
  output [15:0] Result,
  output Overflow
);


  assign Overflow = N1[0];
  assign Result = {N1[0], N1[15:1]};

  // Notes on the sheet:
  //   ROTACION A  LA DERECHA
endmodule

module SL (
  input  [15:0] N1,
  output [15:0] Result,
  output Overflow
);


  assign Overflow = N1[15];
  assign Result = {N1[14:0], 1'b0};
endmodule

module RL (
  input  [15:0] N1,
  output [15:0] Result,
  output Overflow
);


  assign Overflow = N1[15];
  assign Result = {N1[14:0], N1[15]};

  // Notes on the sheet:
  //   ROTACION A LA IZQUIERDA
endmodule

module SLT (
  input  [15:0] N1,
  input  [15:0] N2,
  output Bbit
);

  Comparator #(.width(16)) comparator_1 (.a(N1), .b(N2), .lt(Bbit));  // open: gt, eq
endmodule

module SGT (
  input  [15:0] N1,
  input  [15:0] N2,
  output Bbit
);

  Comparator #(.width(16)) comparator_1 (.a(N1), .b(N2), .gt(Bbit));  // open: eq, lt

  // Notes on the sheet:
  //   COMPARACION DEMAYOR QUE
endmodule

module EQ (
  input  [15:0] N1,
  input  [15:0] N2,
  output Branchbit
);

  wire comparator_1_eq, comparator_2_eq, comparator_3_eq, comparator_4_eq, comparator_5_eq, comparator_6_eq,
       comparator_7_eq, comparator_8_eq, comparator_9_eq, comparator_10_eq, comparator_11_eq,
       comparator_12_eq, comparator_13_eq, comparator_14_eq, comparator_15_eq, comparator_16_eq;

  Comparator #(.width(1)) comparator_1 (.a(N1[0]), .b(N2[0]), .eq(comparator_1_eq));  // open: gt, lt
  Comparator #(.width(1)) comparator_2 (.a(N1[1]), .b(N2[1]), .eq(comparator_2_eq));  // open: gt, lt
  Comparator #(.width(1)) comparator_3 (.a(N1[2]), .b(N2[2]), .eq(comparator_3_eq));  // open: gt, lt
  Comparator #(.width(1)) comparator_4 (.a(N1[3]), .b(N2[3]), .eq(comparator_4_eq));  // open: gt, lt
  Comparator #(.width(1)) comparator_5 (.a(N1[4]), .b(N2[4]), .eq(comparator_5_eq));  // open: gt, lt
  Comparator #(.width(1)) comparator_6 (.a(N1[5]), .b(N2[5]), .eq(comparator_6_eq));  // open: gt, lt
  Comparator #(.width(1)) comparator_7 (.a(N1[6]), .b(N2[6]), .eq(comparator_7_eq));  // open: gt, lt
  Comparator #(.width(1)) comparator_8 (.a(N1[7]), .b(N2[7]), .eq(comparator_8_eq));  // open: gt, lt
  Comparator #(.width(1)) comparator_9 (.a(N1[8]), .b(N2[8]), .eq(comparator_9_eq));  // open: gt, lt
  Comparator #(.width(1)) comparator_10 (.a(N1[9]), .b(N2[9]), .eq(comparator_10_eq));  // open: gt, lt
  Comparator #(.width(1)) comparator_11 (.a(N1[10]), .b(N2[10]), .eq(comparator_11_eq));  // open: gt, lt
  Comparator #(.width(1)) comparator_12 (.a(N1[11]), .b(N2[11]), .eq(comparator_12_eq));  // open: gt, lt
  Comparator #(.width(1)) comparator_13 (.a(N1[12]), .b(N2[12]), .eq(comparator_13_eq));  // open: gt, lt
  Comparator #(.width(1)) comparator_14 (.a(N1[13]), .b(N2[13]), .eq(comparator_14_eq));  // open: gt, lt
  Comparator #(.width(1)) comparator_15 (.a(N1[14]), .b(N2[14]), .eq(comparator_15_eq));  // open: gt, lt
  Comparator #(.width(1)) comparator_16 (.a(N1[15]), .b(N2[15]), .eq(comparator_16_eq));  // open: gt, lt
  and and_1 (Branchbit, comparator_1_eq, comparator_2_eq, comparator_3_eq, comparator_4_eq, comparator_5_eq, comparator_6_eq, comparator_7_eq, comparator_8_eq, comparator_9_eq, comparator_10_eq, comparator_11_eq, comparator_12_eq, comparator_13_eq, comparator_14_eq, comparator_15_eq, comparator_16_eq);
endmodule

module ALU (
  input  [3:0] NEM,
  input  [3:0] RD,
  input  [15:0] RS2,
  input  [15:0] RS1,
  output [15:0] Result,
  output Bbit
);

  wire demultiplexer_1_out0, demultiplexer_1_out1, demultiplexer_1_out2, demultiplexer_1_out3,
       demultiplexer_1_out4, demultiplexer_1_out5, demultiplexer_1_out6, demultiplexer_1_out7,
       eq_1_branchbit, multiplexer_7_out, multiplexer_8_out, not_1_out, sgt_1_bbit, slt_1_bbit;
  wire [15:0] add_1_result, and_1_re, divider_1_out, divider_1_rem, multiplexer_1_out, multiplexer_2_out,
       multiplexer_3_out, multiplexer_4_out, multiplexer_5_out, multiplexer_6_out, multiplier_1_out, or_1_re,
       rl_1_result, rr_1_result, sl_1_result, sr_1_result, sub_1_out_3, xor_1_resp;

  ADD add_1 (.B(RS2), .A(RS1), .Result(add_1_result));  // open: out_4
  Multiplexer #(.width(16), .enable("false")) multiplexer_1 (
    .in0(add_1_result), .in1(multiplier_1_out), .out(multiplexer_1_out), .sel(RD[0]));
  Multiplier #(.width(16)) multiplier_1 (.a(RS2), .b(RS1), .out(multiplier_1_out));  // open: cin, cout
  SUB sub_1 (.S(RS2), .M(RS1), .out_3(sub_1_out_3));  // open: Borrow
  Multiplexer #(.width(16), .enable("false")) multiplexer_2 (
    .in0(sub_1_out_3), .in1(divider_1_out), .out(multiplexer_2_out), .sel(RD[0]));
  Divider #(.width(16)) divider_1 (.a(RS1), .b(RS2), .out(divider_1_out), .rem(divider_1_rem));  // open: upper
  AND and_1 (.R1(RS1), .R2(RS2), .Re(and_1_re));
  Multiplexer #(.width(16), .enable("false")) multiplexer_3 (
    .in0(and_1_re), .in1(divider_1_rem), .out(multiplexer_3_out), .sel(RD[0]));
  OR or_1 (.R1(RS1), .R2(RS2), .Re(or_1_re));
  Multiplexer #(.width(16), .enable("false")) multiplexer_4 (
    .in0(or_1_re), .in1(xor_1_resp), .out(multiplexer_4_out), .sel(RD[0]));
  XOR xor_1 (.in_1(RS1), .in_2(RS2), .Resp(xor_1_resp));
  SR sr_1 (.N1(RS1), .Result(sr_1_result));  // open: Overflow
  Multiplexer #(.width(16), .enable("false")) multiplexer_5 (
    .in0(sr_1_result), .in1(rr_1_result), .out(multiplexer_5_out), .sel(RD[0]));
  RR rr_1 (.N1(RS1), .Result(rr_1_result));  // open: Overflow
  SL sl_1 (.N1(RS1), .Result(sl_1_result));  // open: Overflow
  Multiplexer #(.width(16), .enable("false")) multiplexer_6 (
    .in0(sl_1_result), .in1(rl_1_result), .out(multiplexer_6_out), .sel(RD[0]));
  RL rl_1 (.N1(RS1), .Result(rl_1_result));  // open: Overflow
  SLT slt_1 (.N1(RS1), .N2(RS2), .Bbit(slt_1_bbit));
  Multiplexer #(.enable("false")) multiplexer_7 (
    .in0(slt_1_bbit), .in1(sgt_1_bbit), .out(multiplexer_7_out), .sel(RD[0]));
  SGT sgt_1 (.N1(RS1), .N2(RS2), .Bbit(sgt_1_bbit));
  EQ eq_1 (.N1(RS1), .N2(RS2), .Branchbit(eq_1_branchbit));
  Multiplexer #(.enable("false")) multiplexer_8 (
    .in0(eq_1_branchbit), .in1(not_1_out), .out(multiplexer_8_out), .sel(RD[0]));
  not not_1 (not_1_out, eq_1_branchbit);
  assign Result = demultiplexer_1_out0 ? multiplexer_1_out : 16'bz;  // Controlled_Buffer controlled_buffer_1
  assign Result = demultiplexer_1_out1 ? multiplexer_2_out : 16'bz;  // Controlled_Buffer controlled_buffer_2
  assign Result = demultiplexer_1_out2 ? multiplexer_3_out : 16'bz;  // Controlled_Buffer controlled_buffer_3
  assign Result = demultiplexer_1_out3 ? multiplexer_4_out : 16'bz;  // Controlled_Buffer controlled_buffer_4
  assign Result = demultiplexer_1_out4 ? multiplexer_5_out : 16'bz;  // Controlled_Buffer controlled_buffer_5
  assign Result = demultiplexer_1_out5 ? multiplexer_6_out : 16'bz;  // Controlled_Buffer controlled_buffer_6
  assign Bbit = demultiplexer_1_out6 ? multiplexer_7_out : 1'bz;  // Controlled_Buffer controlled_buffer_7
  assign Bbit = demultiplexer_1_out7 ? multiplexer_8_out : 1'bz;  // Controlled_Buffer controlled_buffer_8
  Demultiplexer #(.select(4), .enable("false")) demultiplexer_1 (
    .out0(demultiplexer_1_out0), .out1(demultiplexer_1_out1), .out2(demultiplexer_1_out2),
    .out3(demultiplexer_1_out3), .out4(demultiplexer_1_out4), .out5(demultiplexer_1_out5),
    .out6(demultiplexer_1_out6), .out7(demultiplexer_1_out7), .in(1'b1), .sel(NEM));  // open: out8, out9, out10, out11, out12, out13, out14, out15

  // Notes on the sheet:
  //   UNIDAD ARITMETICA Y LOGICA
  //   Datos del estudiante
  //   Abdiel Mendoza
  //   3-749-1302
  //   1LS-132
endmodule

// MEN
module MEM (
  input  [3:0] NEM,
  input  [3:0] RF1,
  input  [3:0] RF2,
  input  [3:0] RD,
  input  [15:0] Direccion_RF1,
  input  [15:0] Guardar_RF2,
  input  [15:0] Redest_RD,
  output [15:0] Resultados,
  output [15:0] Address_RF1,
  output [15:0] Store_RF2,
  output actR
);

  wire demultiplexer_1_out8, demultiplexer_1_out9, demultiplexer_1_out10, demultiplexer_1_out11, sb_1_sb;
  wire [15:0] controlled_buffer_6_out, li_1_result, lui_1_result, multiplexer_1_out, multiplexer_2_out,
       swp_1_result, undriven;

  Multiplexer #(.width(16), .enable("false")) multiplexer_1 (
    .in0(Guardar_RF2), .in1(undriven), .out(multiplexer_1_out), .sel(sb_1_sb));
  SWP swp_1 (.Result(swp_1_result), .RN1(Direccion_RF1));
  assign Address_RF1 = sb_1_sb ? Direccion_RF1 : 16'bz;  // Controlled_Buffer controlled_buffer_1
  assign actR = sb_1_sb ? 1'b1 : 1'bz;  // Controlled_Buffer controlled_buffer_2
  assign Store_RF2 = sb_1_sb ? Guardar_RF2 : 16'bz;  // Controlled_Buffer controlled_buffer_3
  assign Resultados = demultiplexer_1_out8 ? multiplexer_1_out : 16'bz;  // Controlled_Buffer controlled_buffer_4
  assign Address_RF1 = demultiplexer_1_out9 ? Direccion_RF1 : 16'bz;  // Controlled_Buffer controlled_buffer_5
  assign controlled_buffer_6_out = demultiplexer_1_out9 ? Redest_RD : 16'bz;  // Controlled_Buffer controlled_buffer_6
  Demultiplexer #(.select(4), .enable("false")) demultiplexer_1 (
    .out8(demultiplexer_1_out8), .out9(demultiplexer_1_out9), .out10(demultiplexer_1_out10),
    .out11(demultiplexer_1_out11), .in(1'b1), .sel(NEM));  // open: out0, out1, out2, out3, out4, out5, out6, out7, out12, out13, out14, out15
  LI li_1 (.Rdc1(RF1), .Rdc2(RF2), .Result(li_1_result));
  assign Resultados = demultiplexer_1_out10 ? li_1_result : 16'bz;  // Controlled_Buffer controlled_buffer_7
  LUI lui_1 (.Rdc1(RF1), .Rdc2(RF2), .Result(lui_1_result), .Rlow(Guardar_RF2));
  assign Resultados = demultiplexer_1_out11 ? lui_1_result : 16'bz;  // Controlled_Buffer controlled_buffer_8
  Multiplexer #(.width(16), .enable("false")) multiplexer_2 (
    .in0(controlled_buffer_6_out), .in1(swp_1_result), .out(multiplexer_2_out), .sel(RD[0]));
  assign Resultados = demultiplexer_1_out9 ? multiplexer_2_out : 16'bz;  // Controlled_Buffer controlled_buffer_9
  SB sb_1 (.RD(RD[0]), .NM(demultiplexer_1_out8), .SB(sb_1_sb));
  assign actR = demultiplexer_1_out9 ? 1'b0 : 1'bz;  // Controlled_Buffer controlled_buffer_10

  // Notes on the sheet:
  //   ADMINISTRADOR DE MEMORIA
  //   Datos del estudiante
  //   Abdiel Mendoza
  //   3-749-1302
  //   1LS-132
endmodule

module JMP (
  input  [3:0] NEM,
  input  [3:0] RF2,
  input  [3:0] RF1,
  input  [3:0] RD,
  input  Bbit,
  input  [15:0] RF1_2,
  input  [15:0] PC,
  output [15:0] Imm,
  output Jact,
  output [15:0] PCdata,
  output CLS
);

  wire and_1_out, demultiplexer_1_out12, demultiplexer_1_out13, demultiplexer_1_out14, demultiplexer_1_out15,
       jr_bbr_1_s;
  wire [15:0] multiplexer_1_out;

  JR_BBR jr_bbr_1 (.RD_2(RD[0]), .BB(Bbit), .NM(demultiplexer_1_out14), .S(jr_bbr_1_s), .RD(RD));
  Demultiplexer #(.select(4), .enable("false")) demultiplexer_1 (
    .out12(demultiplexer_1_out12), .out13(demultiplexer_1_out13), .out14(demultiplexer_1_out14),
    .out15(demultiplexer_1_out15), .in(1'b1), .sel(NEM));  // open: out0, out1, out2, out3, out4, out5, out6, out7, out8, out9, out10, out11
  assign Imm = demultiplexer_1_out12 ? {4'b0000, RD, RF1, RF2} : 16'bz;  // Controlled_Buffer controlled_buffer_1
  assign Jact = demultiplexer_1_out12 ? 1'b1 : 1'bz;  // Controlled_Buffer controlled_buffer_2
  assign Imm = and_1_out ? {4'b0000, RD, RF1, RF2} : 16'bz;  // Controlled_Buffer controlled_buffer_3
  assign Jact = and_1_out ? 1'b1 : 1'bz;  // Controlled_Buffer controlled_buffer_4
  and and_1 (and_1_out, demultiplexer_1_out13, Bbit);
  assign Jact = jr_bbr_1_s ? 1'b1 : 1'bz;  // Controlled_Buffer controlled_buffer_5
  assign Imm = jr_bbr_1_s ? RF1_2 : 16'bz;  // Controlled_Buffer controlled_buffer_6
  Multiplexer #(.width(16), .enable("false")) multiplexer_1 (
    .in0(PC), .out(multiplexer_1_out), .sel(RD[0]));  // open: in1
  assign PCdata = demultiplexer_1_out15 ? multiplexer_1_out : 16'bz;  // Controlled_Buffer controlled_buffer_7
  assign CLS = demultiplexer_1_out15 ? RD[0] : 1'bz;  // Controlled_Buffer controlled_buffer_8

  // Notes on the sheet:
  //   SALTOS DIRECTOS E INDIRECTOS
  //   Datos del estudiante
  //   Abdiel Mendoza
  //   3-749-1302
  //   1LS-132
endmodule

module JR_BBR (
  input  [3:0] RD,
  input  RD_2,
  input  BB,
  input  NM,
  output S
);

  wire and_1_out, comparator_1_eq, not_1_out, not_2_out, or_1_out;

  Comparator #(.width(4)) comparator_1 (.a(RD), .b(4'b0001), .eq(comparator_1_eq));  // open: gt, lt
  not not_1 (not_1_out, RD_2);
  or or_1 (or_1_out, not_1_out, BB);
  and and_1 (and_1_out, NM, or_1_out);
  not not_2 (not_2_out, comparator_1_eq);
  and and_2 (S, and_1_out, not_2_out);
endmodule

module SB (
  input  RD,
  input  NM,
  output SB
);

  wire not_1_out;

  not not_1 (not_1_out, RD);
  and and_1 (SB, NM, not_1_out);
endmodule

module LUI (
  input  [3:0] Rdc1,
  input  [15:0] Rlow,
  input  [3:0] Rdc2,
  output [15:0] Result
);


  assign Result = {Rdc1, Rdc2, Rlow[7:0]};

  // Notes on the sheet:
  //   ALMACENAMIENTO PARTE ALTA
endmodule

module LI (
  input  [3:0] Rdc1,
  input  [3:0] Rdc2,
  output [15:0] Result
);


  assign Result = {{8{1'b0}}, Rdc1, Rdc2};
endmodule

module SWP (
  input  [15:0] RN1,
  output [15:0] Result
);


  assign Result = {RN1[7:0], RN1[15:8]};

  // Notes on the sheet:
  //   INTERCAMBIO BAJA <-> ALTA
endmodule

// REG
module REG_S (
  input  [15:0] DataR,
  input  Bbit,
  input  [6:0] ASCII,
  input  [3:0] RF1,
  input  [3:0] RF2,
  input  [3:0] NEM,
  input  CLOCK,
  input  [3:0] RD,
  output [15:0] Rsrc2,
  output B8,
  output B7,
  output [6:0] Salida,
  output [15:0] Rsrc1
);

  wire demultiplexer_1_out0, demultiplexer_1_out1, demultiplexer_1_out2, demultiplexer_1_out3,
       demultiplexer_1_out4, demultiplexer_1_out5, demultiplexer_1_out6, demultiplexer_1_out7,
       demultiplexer_1_out8, demultiplexer_1_out9, demultiplexer_1_out10, demultiplexer_1_out11,
       demultiplexer_1_out12, demultiplexer_1_out13, demultiplexer_1_out14, demultiplexer_1_out15, rst_1_rst;
  wire [3:0] mov_lui_1_out_5, mov_lui_1_out_6, R0_2_out_2, R0_2_out_3, R0_2_out_4, R0_2_out_5, R0_2_out_6,
       R1_2_out_2, R1_2_out_3, R1_2_out_4, R1_2_out_5, R1_2_out_6, R2_2_out_2, R2_2_out_3, R2_2_out_4,
       R2_2_out_5, R2_2_out_6, R3_2_out_2, R3_2_out_3, R3_2_out_4, R3_2_out_5, R3_2_out_6, R4_2_out_2,
       R4_2_out_3, R4_2_out_4, R4_2_out_5, R4_2_out_6, R5_2_out_2, R5_2_out_3, R5_2_out_4, R5_2_out_5,
       R5_2_out_6, R6_2_out_2, R6_2_out_3, R6_2_out_4, R6_2_out_5, R6_2_out_6, R7_2_out_2, R7_2_out_3,
       R7_2_out_4, R7_2_out_5, R7_2_out_6, R8_2_out_2, R8_2_out_3, R8_2_out_4, R8_2_out_5, R8_2_out_6,
       R9_2_out_2, R9_2_out_3, R9_2_out_4, R9_2_out_5, R9_2_out_6, R10_2_out_2, R10_2_out_3, R10_2_out_4,
       R10_2_out_5, R10_2_out_6, R11_2_out_2, R11_2_out_3, R11_2_out_4, R11_2_out_5, R11_2_out_6,
       R12_2_out_2, R12_2_out_3, R12_2_out_4, R12_2_out_5, R12_2_out_6, R13_2_out_2, R13_2_out_3,
       R13_2_out_4, R13_2_out_5, R13_2_out_6, R14_2_out_2, R14_2_out_3, R14_2_out_4, R14_2_out_5,
       R14_2_out_6, R15_2_out_2, R15_2_out_3, R15_2_out_4, R15_2_out_5, R15_2_out_6;
  wire [15:0] R0_q, R1_q, R2_q, R3_q, R4_q, R5_q, R6_q, R7_q, R8_q, R9_q, R10_q, R11_q, R12_q, R13_q, R14_q,
       R15_q, tty_key_1_data;

  Demultiplexer #(.select(4), .enable("false")) demultiplexer_1 (
    .out0(demultiplexer_1_out0), .out1(demultiplexer_1_out1), .out2(demultiplexer_1_out2),
    .out3(demultiplexer_1_out3), .out4(demultiplexer_1_out4), .out5(demultiplexer_1_out5),
    .out6(demultiplexer_1_out6), .out7(demultiplexer_1_out7), .out8(demultiplexer_1_out8),
    .out9(demultiplexer_1_out9), .out10(demultiplexer_1_out10), .out11(demultiplexer_1_out11),
    .out12(demultiplexer_1_out12), .out13(demultiplexer_1_out13), .out14(demultiplexer_1_out14),
    .out15(demultiplexer_1_out15), .in(1'b1), .sel(mov_lui_1_out_5));
  TTY_KEY tty_key_1 (
    .Asciitty(Salida), .Data_R(DataR), .R0(R0_q), .Data(tty_key_1_data), .Bit_7(B7), .Asciikey(ASCII),
    .Bbit(Bbit), .Bit_8(B8));
  MOV_LUI mov_lui_1 (.RD(RD), .NEM(NEM), .RF1(RF1), .RF2(RF2), .out_5(mov_lui_1_out_5), .out_6(mov_lui_1_out_6));
  RST rst_1 (.RD(RD), .RST(rst_1_rst), .NEM(NEM));
  Register #(.width(16)) R0 (.D(tty_key_1_data), .en(demultiplexer_1_out0), .Q(R0_q), .clk(CLOCK), .clr(rst_1_rst));
  Register #(.width(16)) R2 (.D(DataR), .en(demultiplexer_1_out2), .Q(R2_q), .clk(CLOCK), .clr(rst_1_rst));
  Register #(.width(16)) R4 (.D(DataR), .en(demultiplexer_1_out4), .Q(R4_q), .clk(CLOCK), .clr(rst_1_rst));
  Register #(.width(16)) R6 (.D(DataR), .en(demultiplexer_1_out6), .Q(R6_q), .clk(CLOCK), .clr(rst_1_rst));
  Register #(.width(16)) R8 (.D(DataR), .en(demultiplexer_1_out8), .Q(R8_q), .clk(CLOCK), .clr(rst_1_rst));
  Register #(.width(16)) R10 (.D(DataR), .en(demultiplexer_1_out10), .Q(R10_q), .clk(CLOCK), .clr(rst_1_rst));
  Register #(.width(16)) R12 (.D(DataR), .en(demultiplexer_1_out12), .Q(R12_q), .clk(CLOCK), .clr(rst_1_rst));
  Register #(.width(16)) R14 (.D(DataR), .en(demultiplexer_1_out14), .Q(R14_q), .clk(CLOCK), .clr(rst_1_rst));
  Register #(.width(16)) R1 (.D(DataR), .en(demultiplexer_1_out1), .Q(R1_q), .clk(CLOCK), .clr(rst_1_rst));
  Register #(.width(16)) R3 (.D(DataR), .en(demultiplexer_1_out3), .Q(R3_q), .clk(CLOCK), .clr(rst_1_rst));
  Register #(.width(16)) R5 (.D(DataR), .en(demultiplexer_1_out5), .Q(R5_q), .clk(CLOCK), .clr(rst_1_rst));
  Register #(.width(16)) R7 (.D(DataR), .en(demultiplexer_1_out7), .Q(R7_q), .clk(CLOCK), .clr(rst_1_rst));
  Register #(.width(16)) R9 (.D(DataR), .en(demultiplexer_1_out9), .Q(R9_q), .clk(CLOCK), .clr(rst_1_rst));
  Register #(.width(16)) R11 (.D(DataR), .en(demultiplexer_1_out11), .Q(R11_q), .clk(CLOCK), .clr(rst_1_rst));
  Register #(.width(16)) R13 (.D(DataR), .en(demultiplexer_1_out13), .Q(R13_q), .clk(CLOCK), .clr(rst_1_rst));
  Register #(.width(16)) R15 (.D(DataR), .en(demultiplexer_1_out15), .Q(R15_q), .clk(CLOCK), .clr(rst_1_rst));
  Hex_Digit_Display hex_digit_display_1 (.value(R0_2_out_2));  // open: dp
  Binario_a_decimal_16_bits R0_2 (
    .in_1(R0_q), .out_2(R0_2_out_2), .out_3(R0_2_out_3), .out_4(R0_2_out_4), .out_5(R0_2_out_5),
    .out_6(R0_2_out_6));
  Hex_Digit_Display hex_digit_display_2 (.value(R3_2_out_2));  // open: dp
  Binario_a_decimal_16_bits R3_2 (
    .in_1(R3_q), .out_2(R3_2_out_2), .out_3(R3_2_out_3), .out_4(R3_2_out_4), .out_5(R3_2_out_5),
    .out_6(R3_2_out_6));
  Hex_Digit_Display hex_digit_display_3 (.value(R10_2_out_2));  // open: dp
  Binario_a_decimal_16_bits R10_2 (
    .in_1(R10_q), .out_2(R10_2_out_2), .out_3(R10_2_out_3), .out_4(R10_2_out_4), .out_5(R10_2_out_5),
    .out_6(R10_2_out_6));
  Hex_Digit_Display hex_digit_display_4 (.value(R13_2_out_2));  // open: dp
  Binario_a_decimal_16_bits R13_2 (
    .in_1(R13_q), .out_2(R13_2_out_2), .out_3(R13_2_out_3), .out_4(R13_2_out_4), .out_5(R13_2_out_5),
    .out_6(R13_2_out_6));
  Hex_Digit_Display hex_digit_display_5 (.value(R0_2_out_3));  // open: dp
  Hex_Digit_Display hex_digit_display_6 (.value(R0_2_out_4));  // open: dp
  Hex_Digit_Display hex_digit_display_7 (.value(R3_2_out_4));  // open: dp
  Hex_Digit_Display hex_digit_display_8 (.value(R3_2_out_3));  // open: dp
  Multiplexer #(.select(4), .width(16), .enable("false")) multiplexer_1 (
    .in0(R0_q), .in1(R1_q), .in2(R2_q), .in3(R3_q), .in4(R4_q), .in5(R5_q), .in6(R6_q), .in7(R7_q),
    .in8(R8_q), .in9(R9_q), .in10(R10_q), .in11(R11_q), .in12(R12_q), .in13(R13_q), .in14(R14_q),
    .in15(R15_q), .out(Rsrc2), .sel(mov_lui_1_out_6));
  Multiplexer #(.select(4), .width(16), .enable("false")) multiplexer_2 (
    .in0(R0_q), .in1(R1_q), .in2(R2_q), .in3(R3_q), .in4(R4_q), .in5(R5_q), .in6(R6_q), .in7(R7_q),
    .in8(R8_q), .in9(R9_q), .in10(R10_q), .in11(R11_q), .in12(R12_q), .in13(R13_q), .in14(R14_q),
    .in15(R15_q), .out(Rsrc1), .sel(RF1));
  Hex_Digit_Display hex_digit_display_9 (.value(R10_2_out_4));  // open: dp
  Hex_Digit_Display hex_digit_display_10 (.value(R10_2_out_3));  // open: dp
  Hex_Digit_Display hex_digit_display_11 (.value(R13_2_out_4));  // open: dp
  Hex_Digit_Display hex_digit_display_12 (.value(R13_2_out_3));  // open: dp
  Hex_Digit_Display hex_digit_display_13 (.value(R0_2_out_5));  // open: dp
  Hex_Digit_Display hex_digit_display_14 (.value(R0_2_out_6));  // open: dp
  Hex_Digit_Display hex_digit_display_15 (.value(R3_2_out_6));  // open: dp
  Hex_Digit_Display hex_digit_display_16 (.value(R3_2_out_5));  // open: dp
  Hex_Digit_Display hex_digit_display_17 (.value(R10_2_out_5));  // open: dp
  Hex_Digit_Display hex_digit_display_18 (.value(R10_2_out_6));  // open: dp
  Hex_Digit_Display hex_digit_display_19 (.value(R13_2_out_6));  // open: dp
  Hex_Digit_Display hex_digit_display_20 (.value(R13_2_out_5));  // open: dp
  Hex_Digit_Display hex_digit_display_21 (.value(R1_2_out_3));  // open: dp
  Hex_Digit_Display hex_digit_display_22 (.value(R1_2_out_2));  // open: dp
  Binario_a_decimal_16_bits R1_2 (
    .in_1(R1_q), .out_2(R1_2_out_2), .out_3(R1_2_out_3), .out_4(R1_2_out_4), .out_5(R1_2_out_5),
    .out_6(R1_2_out_6));
  Hex_Digit_Display hex_digit_display_23 (.value(R4_2_out_2));  // open: dp
  Hex_Digit_Display hex_digit_display_24 (.value(R4_2_out_3));  // open: dp
  Binario_a_decimal_16_bits R4_2 (
    .in_1(R4_q), .out_2(R4_2_out_2), .out_3(R4_2_out_3), .out_4(R4_2_out_4), .out_5(R4_2_out_5),
    .out_6(R4_2_out_6));
  Hex_Digit_Display hex_digit_display_25 (.value(R6_2_out_3));  // open: dp
  Hex_Digit_Display hex_digit_display_26 (.value(R6_2_out_2));  // open: dp
  Binario_a_decimal_16_bits R6_2 (
    .in_1(R6_q), .out_2(R6_2_out_2), .out_3(R6_2_out_3), .out_4(R6_2_out_4), .out_5(R6_2_out_5),
    .out_6(R6_2_out_6));
  Hex_Digit_Display hex_digit_display_27 (.value(R8_2_out_2));  // open: dp
  Hex_Digit_Display hex_digit_display_28 (.value(R8_2_out_3));  // open: dp
  Binario_a_decimal_16_bits R8_2 (
    .in_1(R8_q), .out_2(R8_2_out_2), .out_3(R8_2_out_3), .out_4(R8_2_out_4), .out_5(R8_2_out_5),
    .out_6(R8_2_out_6));
  Hex_Digit_Display hex_digit_display_29 (.value(R11_2_out_3));  // open: dp
  Hex_Digit_Display hex_digit_display_30 (.value(R11_2_out_2));  // open: dp
  Binario_a_decimal_16_bits R11_2 (
    .in_1(R11_q), .out_2(R11_2_out_2), .out_3(R11_2_out_3), .out_4(R11_2_out_4), .out_5(R11_2_out_5),
    .out_6(R11_2_out_6));
  Hex_Digit_Display hex_digit_display_31 (.value(R14_2_out_3));  // open: dp
  Hex_Digit_Display hex_digit_display_32 (.value(R14_2_out_2));  // open: dp
  Binario_a_decimal_16_bits R14_2 (
    .in_1(R14_q), .out_2(R14_2_out_2), .out_3(R14_2_out_3), .out_4(R14_2_out_4), .out_5(R14_2_out_5),
    .out_6(R14_2_out_6));
  Hex_Digit_Display hex_digit_display_33 (.value(R1_2_out_5));  // open: dp
  Hex_Digit_Display hex_digit_display_34 (.value(R1_2_out_4));  // open: dp
  Hex_Digit_Display hex_digit_display_35 (.value(R4_2_out_5));  // open: dp
  Hex_Digit_Display hex_digit_display_36 (.value(R4_2_out_4));  // open: dp
  Hex_Digit_Display hex_digit_display_37 (.value(R6_2_out_4));  // open: dp
  Hex_Digit_Display hex_digit_display_38 (.value(R6_2_out_5));  // open: dp
  Hex_Digit_Display hex_digit_display_39 (.value(R8_2_out_4));  // open: dp
  Hex_Digit_Display hex_digit_display_40 (.value(R8_2_out_5));  // open: dp
  Hex_Digit_Display hex_digit_display_41 (.value(R11_2_out_5));  // open: dp
  Hex_Digit_Display hex_digit_display_42 (.value(R11_2_out_4));  // open: dp
  Hex_Digit_Display hex_digit_display_43 (.value(R14_2_out_4));  // open: dp
  Hex_Digit_Display hex_digit_display_44 (.value(R14_2_out_5));  // open: dp
  Hex_Digit_Display hex_digit_display_45 (.value(R2_2_out_2));  // open: dp
  Hex_Digit_Display hex_digit_display_46 (.value(R1_2_out_6));  // open: dp
  Binario_a_decimal_16_bits R2_2 (
    .in_1(R2_q), .out_2(R2_2_out_2), .out_3(R2_2_out_3), .out_4(R2_2_out_4), .out_5(R2_2_out_5),
    .out_6(R2_2_out_6));
  Hex_Digit_Display hex_digit_display_47 (.value(R4_2_out_6));  // open: dp
  Hex_Digit_Display hex_digit_display_48 (.value(R5_2_out_2));  // open: dp
  Binario_a_decimal_16_bits R5_2 (
    .in_1(R5_q), .out_2(R5_2_out_2), .out_3(R5_2_out_3), .out_4(R5_2_out_4), .out_5(R5_2_out_5),
    .out_6(R5_2_out_6));
  Hex_Digit_Display hex_digit_display_49 (.value(R6_2_out_6));  // open: dp
  Hex_Digit_Display hex_digit_display_50 (.value(R7_2_out_2));  // open: dp
  Binario_a_decimal_16_bits R7_2 (
    .in_1(R7_q), .out_2(R7_2_out_2), .out_3(R7_2_out_3), .out_4(R7_2_out_4), .out_5(R7_2_out_5),
    .out_6(R7_2_out_6));
  Hex_Digit_Display hex_digit_display_51 (.value(R8_2_out_6));  // open: dp
  Hex_Digit_Display hex_digit_display_52 (.value(R9_2_out_2));  // open: dp
  Binario_a_decimal_16_bits R9_2 (
    .in_1(R9_q), .out_2(R9_2_out_2), .out_3(R9_2_out_3), .out_4(R9_2_out_4), .out_5(R9_2_out_5),
    .out_6(R9_2_out_6));
  Hex_Digit_Display hex_digit_display_53 (.value(R11_2_out_6));  // open: dp
  Hex_Digit_Display hex_digit_display_54 (.value(R12_2_out_2));  // open: dp
  Binario_a_decimal_16_bits R12_2 (
    .in_1(R12_q), .out_2(R12_2_out_2), .out_3(R12_2_out_3), .out_4(R12_2_out_4), .out_5(R12_2_out_5),
    .out_6(R12_2_out_6));
  Hex_Digit_Display hex_digit_display_55 (.value(R15_2_out_2));  // open: dp
  Hex_Digit_Display hex_digit_display_56 (.value(R14_2_out_6));  // open: dp
  Binario_a_decimal_16_bits R15_2 (
    .in_1(R15_q), .out_2(R15_2_out_2), .out_3(R15_2_out_3), .out_4(R15_2_out_4), .out_5(R15_2_out_5),
    .out_6(R15_2_out_6));
  Hex_Digit_Display hex_digit_display_57 (.value(R2_2_out_4));  // open: dp
  Hex_Digit_Display hex_digit_display_58 (.value(R2_2_out_3));  // open: dp
  Hex_Digit_Display hex_digit_display_59 (.value(R5_2_out_3));  // open: dp
  Hex_Digit_Display hex_digit_display_60 (.value(R5_2_out_4));  // open: dp
  Hex_Digit_Display hex_digit_display_61 (.value(R7_2_out_3));  // open: dp
  Hex_Digit_Display hex_digit_display_62 (.value(R7_2_out_4));  // open: dp
  Hex_Digit_Display hex_digit_display_63 (.value(R9_2_out_4));  // open: dp
  Hex_Digit_Display hex_digit_display_64 (.value(R9_2_out_3));  // open: dp
  Hex_Digit_Display hex_digit_display_65 (.value(R12_2_out_3));  // open: dp
  Hex_Digit_Display hex_digit_display_66 (.value(R12_2_out_4));  // open: dp
  Hex_Digit_Display hex_digit_display_67 (.value(R15_2_out_4));  // open: dp
  Hex_Digit_Display hex_digit_display_68 (.value(R15_2_out_3));  // open: dp
  Hex_Digit_Display hex_digit_display_69 (.value(R2_2_out_6));  // open: dp
  Hex_Digit_Display hex_digit_display_70 (.value(R2_2_out_5));  // open: dp
  Hex_Digit_Display hex_digit_display_71 (.value(R5_2_out_5));  // open: dp
  Hex_Digit_Display hex_digit_display_72 (.value(R5_2_out_6));  // open: dp
  Hex_Digit_Display hex_digit_display_73 (.value(R7_2_out_6));  // open: dp
  Hex_Digit_Display hex_digit_display_74 (.value(R7_2_out_5));  // open: dp
  Hex_Digit_Display hex_digit_display_75 (.value(R9_2_out_5));  // open: dp
  Hex_Digit_Display hex_digit_display_76 (.value(R9_2_out_6));  // open: dp
  Hex_Digit_Display hex_digit_display_77 (.value(R12_2_out_6));  // open: dp
  Hex_Digit_Display hex_digit_display_78 (.value(R12_2_out_5));  // open: dp
  Hex_Digit_Display hex_digit_display_79 (.value(R15_2_out_5));  // open: dp
  Hex_Digit_Display hex_digit_display_80 (.value(R15_2_out_6));  // open: dp

  // Notes on the sheet:
  //   REGISTROS
  //   Datos del estudiante
  //   Abdiel Mendoza
  //   3-749-1302
  //   1LS-132
endmodule

// TT-KEY
module TTY_KEY (
  input  [15:0] Data_R,
  input  [15:0] R0,
  input  [6:0] Asciikey,
  input  Bbit,
  output [15:0] Data,
  output [6:0] Asciitty,
  output Bit_7,
  output Bit_8
);

  wire and_1_out;

  Multiplexer #(.width(16), .enable("false")) multiplexer_1 (
    .in0(Data_R), .in1({{7{1'b0}}, {2{Bbit}}, Asciikey}), .out(Data), .sel(and_1_out));
  and and_1 (and_1_out, ~Bbit, R0[8]);  // AND_Gate

  assign Asciitty = R0[6:0];
  assign Bit_7 = R0[7];
  assign Bit_8 = R0[8];

  // Notes on the sheet:
  //   Datos del estudiante
  //   Abdiel Mendoza
  //   3-749-1302
  //   1LS-132
endmodule

module RST (
  input  [3:0] RD,
  input  [3:0] NEM,
  output RST
);

  wire comparator_1_eq, comparator_2_eq;

  Comparator #(.width(4)) comparator_1 (.a(NEM), .b(4'b1110), .eq(comparator_1_eq));  // open: gt, lt
  Comparator #(.width(4)) comparator_2 (.a(RD), .b(4'b0001), .eq(comparator_2_eq));  // open: gt, lt
  and and_1 (RST, comparator_2_eq, comparator_1_eq);

  // Notes on the sheet:
  //   Datos del estudiante
  //   Abdiel Mendoza
  //   3-749-1302
  //   1LS-132
endmodule

module MOV_LUI (
  input  [3:0] RF2,
  input  [3:0] NEM,
  input  [3:0] RF1,
  input  [3:0] RD,
  output [3:0] out_5,
  output [3:0] out_6
);

  wire and_1_out, comparator_1_eq, comparator_2_eq;

  Comparator #(.width(4)) comparator_1 (.a(4'b1000), .b(NEM), .eq(comparator_1_eq));  // open: gt, lt
  and and_1 (and_1_out, comparator_1_eq, RD[0]);
  Multiplexer #(.width(4), .enable("false")) multiplexer_1 (.in0(RD), .in1(RF1), .out(out_5), .sel(and_1_out));
  Comparator #(.width(4)) comparator_2 (.a(4'b1011), .b(NEM), .eq(comparator_2_eq));  // open: gt, lt
  Multiplexer #(.width(4), .enable("false")) multiplexer_2 (.in0(RF2), .in1(RD), .out(out_6), .sel(comparator_2_eq));

  // Notes on the sheet:
  //   Datos del estudiante
  //   Abdiel Mendoza
  //   3-749-1302
  //   1LS-132
endmodule

module Binario_a_decimal_16_bits (
  input  [15:0] in_1,
  output [3:0] out_2,
  output [3:0] out_3,
  output [3:0] out_4,
  output [3:0] out_5,
  output [3:0] out_6
);

  wire [15:0] divider_1_out, divider_1_rem, divider_2_out, divider_2_rem, divider_3_out, divider_3_rem,
       divider_4_out, divider_4_rem;

  Divider #(.width(16)) divider_1 (.a(in_1), .b(16'h2710), .out(divider_1_out), .rem(divider_1_rem));  // open: upper
  Divider #(.width(16)) divider_2 (
    .a(divider_1_rem), .b(16'h3e8), .out(divider_2_out), .rem(divider_2_rem));  // open: upper
  Divider #(.width(16)) divider_3 (
    .a(divider_2_rem), .b(16'h64), .out(divider_3_out), .rem(divider_3_rem));  // open: upper
  Divider #(.width(16)) divider_4 (
    .a(divider_3_rem), .b(16'ha), .out(divider_4_out), .rem(divider_4_rem));  // open: upper
  Bit_Extender #(.in_width(16), .out_width(4)) bit_extender_1 (.in(divider_1_out), .out(out_2));
  Bit_Extender #(.in_width(16), .out_width(4)) bit_extender_2 (.in(divider_2_out), .out(out_3));
  Bit_Extender #(.in_width(16), .out_width(4)) bit_extender_3 (.in(divider_3_out), .out(out_4));
  Bit_Extender #(.in_width(16), .out_width(4)) bit_extender_4 (.in(divider_4_out), .out(out_5));
  Bit_Extender #(.in_width(16), .out_width(4)) bit_extender_5 (.in(divider_4_rem), .out(out_6));
endmodule
