// Logisim project ALU.circ as structural Verilog: 13 circuits, main circuit ALU
module ADD (
  input  [15:0] A,
  input  [15:0] B,
  output [15:0] Result,
  output out_4
);

  wire and_1_out, and_2_out, and_3_out, and_4_out, and_5_out, and_6_out, and_7_out, and_8_out, and_9_out,
       and_10_out, and_11_out, and_12_out, and_13_out, and_14_out, and_15_out, and_16_out, and_17_out,
       and_18_out, and_19_out, and_20_out, and_21_out, and_22_out, and_23_out, and_24_out, and_25_out,
       and_26_out, and_27_out, and_28_out, and_29_out, and_30_out, and_31_out, and_32_out, C_2_out, C_3_out,
       C_4_out, C_5_out, C_6_out, C_7_out, C_8_out, C_9_out, C_10_out, C_11_out, C_12_out, C_13_out,
       C_15_out, C_16_out, C_out, xor_1_out, xor_2_out, xor_3_out, xor_4_out, xor_5_out, xor_6_out,
       xor_7_out, xor_8_out, xor_9_out, xor_10_out, xor_11_out, xor_12_out, xor_13_out, xor_14_out,
       xor_15_out, xor_16_out;

  and and_1 (and_1_out, A[0], B[0]);
  and and_2 (and_2_out, A[1], B[1]);
  and and_3 (and_3_out, A[2], B[2]);
  and and_4 (and_4_out, A[4], B[4]);
  and and_5 (and_5_out, A[5], B[5]);
  and and_6 (and_6_out, A[7], B[7]);
  and and_7 (and_7_out, A[8], B[8]);
  and and_8 (and_8_out, A[9], B[9]);
  and and_9 (and_9_out, A[10], B[10]);
  and and_10 (and_10_out, A[11], B[11]);
  and and_11 (and_11_out, A[12], B[12]);
  and and_12 (and_12_out, A[13], B[13]);
  and and_13 (and_13_out, A[14], B[14]);
  and and_14 (and_14_out, A[15], B[15]);
  xor xor_1 (xor_1_out, A[0], B[0]);
  xor xor_2 (xor_2_out, A[1], B[1]);
  xor xor_3 (xor_3_out, A[2], B[2]);
  xor xor_4 (xor_4_out, A[3], B[3]);
  and and_15 (and_15_out, A[3], B[3]);
  xor xor_5 (xor_5_out, A[4], B[4]);
  xor xor_6 (xor_6_out, A[5], B[5]);
  xor xor_7 (xor_7_out, A[6], B[6]);
  and and_16 (and_16_out, A[6], B[6]);
  xor xor_8 (xor_8_out, A[7], B[7]);
  xor xor_9 (xor_9_out, A[8], B[8]);
  xor xor_10 (xor_10_out, A[9], B[9]);
  xor xor_11 (xor_11_out, A[10], B[10]);
  xor xor_12 (xor_12_out, A[11], B[11]);
  xor xor_13 (xor_13_out, A[12], B[12]);
  xor xor_14 (xor_14_out, A[13], B[13]);
  xor xor_15 (xor_15_out, A[14], B[14]);
  xor xor_16 (xor_16_out, A[15], B[15]);
  xor xor_17 (Result[0], xor_1_out, 1'b0);
  or C (C_out, and_17_out, and_1_out);
  and and_17 (and_17_out, xor_1_out, 1'b0);
  xor xor_18 (Result[1], xor_2_out, C_out);
  and and_18 (and_18_out, xor_2_out, C_out);
  or C_2 (C_2_out, and_18_out, and_2_out);
  xor xor_19 (Result[2], xor_3_out, C_2_out);
  or C_3 (C_3_out, and_19_out, and_3_out);
  and and_19 (and_19_out, xor_3_out, C_2_out);
  xor xor_20 (Result[3], xor_4_out, C_3_out);
  and and_20 (and_20_out, xor_4_out, C_3_out);
  xor xor_21 (Result[4], xor_5_out, C_15_out);
  and and_21 (and_21_out, xor_5_out, C_15_out);
  or C_4 (C_4_out, and_21_out, and_4_out);
  xor xor_22 (Result[5], xor_6_out, C_4_out);
  or C_5 (C_5_out, and_22_out, and_5_out);
  and and_22 (and_22_out, xor_6_out, C_4_out);
  xor xor_23 (Result[6], xor_7_out, C_5_out);
  and and_23 (and_23_out, xor_7_out, C_5_out);
  xor xor_24 (Result[7], xor_8_out, C_16_out);
  or C_6 (C_6_out, and_24_out, and_6_out);
  and and_24 (and_24_out, xor_8_out, C_16_out);
  xor xor_25 (Result[8], xor_9_out, C_6_out);
  or C_7 (C_7_out, and_25_out, and_7_out);
  and and_25 (and_25_out, xor_9_out, C_6_out);
  xor xor_26 (Result[9], xor_10_out, C_7_out);
  or C_8 (C_8_out, and_26_out, and_8_out);
  and and_26 (and_26_out, xor_10_out, C_7_out);
  xor xor_27 (Result[10], xor_11_out, C_8_out);
  and and_27 (and_27_out, xor_11_out, C_8_out);
  or C_9 (C_9_out, and_27_out, and_9_out);
  xor xor_28 (Result[11], xor_12_out, C_9_out);
  and and_28 (and_28_out, xor_12_out, C_9_out);
  or C_10 (C_10_out, and_28_out, and_10_out);
  xor xor_29 (Result[12], xor_13_out, C_10_out);
  or C_11 (C_11_out, and_29_out, and_11_out);
  and and_29 (and_29_out, xor_13_out, C_10_out);
  xor xor_30 (Result[13], xor_14_out, C_11_out);
  or C_12 (C_12_out, and_30_out, and_12_out);
  and and_30 (and_30_out, xor_14_out, C_11_out);
  xor xor_31 (Result[14], xor_15_out, C_12_out);
  or C_13 (C_13_out, and_31_out, and_13_out);
  and and_31 (and_31_out, xor_15_out, C_12_out);
  xor xor_32 (Result[15], xor_16_out, C_13_out);
  or C_14 (out_4, and_32_out, and_14_out);
  and and_32 (and_32_out, xor_16_out, C_13_out);
  or C_15 (C_15_out, and_20_out, and_15_out);
  or C_16 (C_16_out, and_23_out, and_16_out);
endmodule

module SUB (
  input  [15:0] M,
  input  [15:0] S,
  output [15:0] out_3,
  output Borrow
);

  wire and_1_out, and_2_out, and_3_out, and_4_out, and_5_out, and_6_out, and_7_out, and_8_out, and_9_out,
       and_10_out, and_11_out, and_12_out, and_13_out, and_14_out, and_15_out, and_16_out, and_17_out,
       and_18_out, and_19_out, and_20_out, and_21_out, and_22_out, and_23_out, and_24_out, and_25_out,
       and_26_out, and_27_out, and_28_out, and_29_out, and_30_out, and_31_out, and_32_out, B_2_out, B_3_out,
       B_4_out, B_5_out, B_6_out, B_7_out, B_8_out, B_9_out, B_10_out, B_11_out, B_12_out, B_13_out,
       B_14_out, B_15_out, B_out, not_1_out, not_2_out, not_3_out, not_4_out, not_5_out, not_6_out,
       not_7_out, not_8_out, not_9_out, not_10_out, not_11_out, not_12_out, not_13_out, not_14_out,
       not_15_out, not_16_out, not_17_out, not_18_out, not_19_out, not_20_out, not_21_out, not_22_out,
       not_23_out, not_24_out, not_25_out, not_26_out, not_27_out, not_28_out, not_29_out, not_30_out,
       not_31_out, not_32_out, xor_1_out, xor_2_out, xor_3_out, xor_4_out, xor_5_out, xor_6_out, xor_7_out,
       xor_8_out, xor_9_out, xor_10_out, xor_11_out, xor_12_out, xor_13_out, xor_14_out, xor_15_out,
       xor_16_out;

  not not_1 (not_1_out, M[12]);
  not not_2 (not_2_out, M[13]);
  not not_3 (not_3_out, M[14]);
  not not_4 (not_4_out, M[15]);
  not not_5 (not_5_out, M[4]);
  not not_6 (not_6_out, M[5]);
  not not_7 (not_7_out, M[6]);
  not not_8 (not_8_out, M[7]);
  not not_9 (not_9_out, M[8]);
  not not_10 (not_10_out, M[9]);
  not not_11 (not_11_out, M[10]);
  not not_12 (not_12_out, M[11]);
  not not_13 (not_13_out, M[0]);
  not not_14 (not_14_out, M[1]);
  not not_15 (not_15_out, M[2]);
  not not_16 (not_16_out, M[3]);
  xor xor_1 (xor_1_out, M[0], S[0]);
  and and_1 (and_1_out, not_13_out, S[0]);
  xor xor_2 (xor_2_out, M[1], S[1]);
  and and_2 (and_2_out, not_14_out, S[1]);
  xor xor_3 (xor_3_out, M[2], S[2]);
  and and_3 (and_3_out, not_15_out, S[2]);
  xor xor_4 (xor_4_out, M[3], S[3]);
  and and_4 (and_4_out, not_16_out, S[3]);
  xor xor_5 (xor_5_out, M[4], S[4]);
  and and_5 (and_5_out, not_5_out, S[4]);
  xor xor_6 (xor_6_out, M[5], S[5]);
  and and_6 (and_6_out, not_6_out, S[5]);
  xor xor_7 (xor_7_out, M[6], S[6]);
  and and_7 (and_7_out, not_7_out, S[6]);
  xor xor_8 (xor_8_out, M[7], S[7]);
  and and_8 (and_8_out, not_8_out, S[7]);
  xor xor_9 (xor_9_out, M[8], S[8]);
  and and_9 (and_9_out, not_9_out, S[8]);
  xor xor_10 (xor_10_out, M[9], S[9]);
  and and_10 (and_10_out, not_10_out, S[9]);
  xor xor_11 (xor_11_out, M[10], S[10]);
  and and_11 (and_11_out, not_11_out, S[10]);
  xor xor_12 (xor_12_out, M[11], S[11]);
  and and_12 (and_12_out, not_12_out, S[11]);
  xor xor_13 (xor_13_out, M[12], S[12]);
  and and_13 (and_13_out, not_1_out, S[12]);
  xor xor_14 (xor_14_out, M[13], S[13]);
  and and_14 (and_14_out, not_2_out, S[13]);
  xor xor_15 (xor_15_out, M[14], S[14]);
  and and_15 (and_15_out, not_3_out, S[14]);
  xor xor_16 (xor_16_out, M[15], S[15]);
  and and_16 (and_16_out, not_4_out, S[15]);
  xor T (out_3[0], xor_1_out, 1'b0);
  not not_17 (not_17_out, xor_1_out);
  and and_17 (and_17_out, not_17_out, 1'b0);
  xor xor_17 (out_3[1], xor_2_out, B_out);
  not not_18 (not_18_out, xor_2_out);
  and and_18 (and_18_out, not_18_out, B_out);
  xor xor_18 (out_3[2], xor_3_out, B_2_out);
  not not_19 (not_19_out, xor_3_out);
  and and_19 (and_19_out, not_19_out, B_2_out);
  xor xor_19 (out_3[3], xor_4_out, B_3_out);
  not not_20 (not_20_out, xor_4_out);
  and and_20 (and_20_out, not_20_out, B_3_out);
  xor xor_20 (out_3[4], xor_5_out, B_4_out);
  not not_21 (not_21_out, xor_5_out);
  and and_21 (and_21_out, not_21_out, B_4_out);
  xor xor_21 (out_3[5], xor_6_out, B_5_out);
  not not_22 (not_22_out, xor_6_out);
  and and_22 (and_22_out, not_22_out, B_5_out);
  xor xor_22 (out_3[6], xor_7_out, B_6_out);
  not not_23 (not_23_out, xor_7_out);
  and and_23 (and_23_out, not_23_out, B_6_out);
  xor xor_23 (out_3[7], xor_8_out, B_7_out);
  not not_24 (not_24_out, xor_8_out);
  and and_24 (and_24_out, not_24_out, B_7_out);
  xor xor_24 (out_3[8], xor_9_out, B_8_out);
  not not_25 (not_25_out, xor_9_out);
  and and_25 (and_25_out, not_25_out, B_8_out);
  xor xor_25 (out_3[9], xor_10_out, B_9_out);
  not not_26 (not_26_out, xor_10_out);
  and and_26 (and_26_out, not_26_out, B_9_out);
  xor xor_26 (out_3[10], xor_11_out, B_10_out);
  not not_27 (not_27_out, xor_11_out);
  and and_27 (and_27_out, not_27_out, B_10_out);
  xor xor_27 (out_3[11], xor_12_out, B_11_out);
  not not_28 (not_28_out, xor_12_out);
  and and_28 (and_28_out, not_28_out, B_11_out);
  xor xor_28 (out_3[12], xor_13_out, B_12_out);
  not not_29 (not_29_out, xor_13_out);
  and and_29 (and_29_out, not_29_out, B_12_out);
  xor xor_29 (out_3[13], xor_14_out, B_13_out);
  not not_30 (not_30_out, xor_14_out);
  and and_30 (and_30_out, not_30_out, B_13_out);
  xor xor_30 (out_3[14], xor_15_out, B_14_out);
  not not_31 (not_31_out, xor_15_out);
  and and_31 (and_31_out, not_31_out, B_14_out);
  xor xor_31 (out_3[15], xor_16_out, B_15_out);
  not not_32 (not_32_out, xor_16_out);
  and and_32 (and_32_out, not_32_out, B_15_out);
  or B (B_out, and_17_out, and_1_out);
  or B_2 (B_2_out, and_18_out, and_2_out);
  or B_3 (B_3_out, and_19_out, and_3_out);
  or B_4 (B_4_out, and_20_out, and_4_out);
  or B_5 (B_5_out, and_21_out, and_5_out);
  or B_6 (B_6_out, and_22_out, and_6_out);
  or B_7 (B_7_out, and_7_out, and_23_out);
  or B_8 (B_8_out, and_8_out, and_24_out);
  or B_9 (B_9_out, and_9_out, and_25_out);
  or B_10 (B_10_out, and_10_out, and_26_out);
  or B_11 (B_11_out, and_11_out, and_27_out);
  or B_12 (B_12_out, and_12_out, and_28_out);
  or B_13 (B_13_out, and_13_out, and_29_out);
  or B_14 (B_14_out, and_14_out, and_30_out);
  or B_15 (B_15_out, and_15_out, and_31_out);
  or B_16 (Borrow, and_16_out, and_32_out);
endmodule

module AND (
  input  [15:0] R1,
  input  [15:0] R2,
  output [15:0] Re
);

  and and_1 (Re[0], R1[0], R2[0]);
  and and_2 (Re[1], R1[1], R2[1]);
  and and_3 (Re[2], R1[2], R2[2]);
  and and_4 (Re[3], R1[3], R2[3]);
  and and_5 (Re[4], R1[4], R2[4]);
  and and_6 (Re[5], R1[5], R2[5]);
  and and_7 (Re[6], R1[6], R2[6]);
  and and_8 (Re[7], R1[7], R2[7]);
  and and_9 (Re[8], R1[8], R2[8]);
  and and_10 (Re[9], R1[9], R2[9]);
  and and_11 (Re[10], R1[10], R2[10]);
  and and_12 (Re[11], R1[11], R2[11]);
  and and_13 (Re[12], R1[12], R2[12]);
  and and_14 (Re[13], R1[13], R2[13]);
  and and_15 (Re[14], R1[14], R2[14]);
  and and_16 (Re[15], R1[15], R2[15]);
endmodule

module OR (
  input  [15:0] R1,
  input  [15:0] R2,
  output [15:0] Re
);

  or or_1 (Re[0], R1[0], R2[0]);
  or or_2 (Re[1], R1[1], R2[1]);
  or or_3 (Re[2], R1[2], R2[2]);
  or or_4 (Re[3], R1[3], R2[3]);
  or or_5 (Re[4], R1[4], R2[4]);
  or or_6 (Re[5], R1[5], R2[5]);
  or or_7 (Re[6], R1[6], R2[6]);
  or or_8 (Re[7], R1[7], R2[7]);
  or or_9 (Re[8], R1[8], R2[8]);
  or or_10 (Re[9], R1[9], R2[9]);
  or or_11 (Re[10], R1[10], R2[10]);
  or or_12 (Re[11], R1[11], R2[11]);
  or or_13 (Re[12], R1[12], R2[12]);
  or or_14 (Re[13], R1[13], R2[13]);
  or or_15 (Re[14], R1[14], R2[14]);
  or or_16 (Re[15], R1[15], R2[15]);
endmodule

module XOR (
  input  [15:0] in_1,
  input  [15:0] in_2,
  output [15:0] Resp
);

  xor xor_1 (Resp[0], in_1[0], in_2[0]);
  xor xor_2 (Resp[1], in_1[1], in_2[1]);
  xor xor_3 (Resp[2], in_1[2], in_2[2]);
  xor xor_4 (Resp[3], in_1[3], in_2[3]);
  xor xor_5 (Resp[4], in_1[4], in_2[4]);
  xor xor_6 (Resp[5], in_1[5], in_2[5]);
  xor xor_7 (Resp[6], in_1[6], in_2[6]);
  xor xor_8 (Resp[7], in_1[7], in_2[7]);
  xor xor_9 (Resp[8], in_1[8], in_2[8]);
  xor xor_10 (Resp[9], in_1[9], in_2[9]);
  xor xor_11 (Resp[10], in_1[10], in_2[10]);
  xor xor_12 (Resp[11], in_1[11], in_2[11]);
  xor xor_13 (Resp[12], in_1[12], in_2[12]);
  xor xor_14 (Resp[13], in_1[13], in_2[13]);
  xor xor_15 (Resp[14], in_1[14], in_2[14]);
  xor xor_16 (Resp[15], in_1[15], in_2[15]);

  // Notes on the sheet:
  //   R1
  //   R2
  //   CIRCUITO XOR
endmodule

module SR (
  input  [15:0] N1,
  output Overflow,
  output [15:0] Result
);


  assign Overflow = N1[0];
  assign Result = {1'b0, N1[15:1]};
endmodule

module RR (
  input  [15:0] N1,
  output [15:0] Result,
  output Overflow
);


  assign Overflow = N1[0];
  assign Result = {N1[0], N1[15:1]};

  // Notes on the sheet:
  //   ROTACION A  LA DERECHA
endmodule

module SL (
  input  [15:0] N1,
  output [15:0] Result,
  output Overflow
);


  assign Overflow = N1[15];
  assign Result = {N1[14:0], 1'b0};
endmodule

module RL (
  input  [15:0] N1,
  output [15:0] Result,
  output Overflow
);


  assign Overflow = N1[15];
  assign Result = {N1[14:0], N1[15]};

  // Notes on the sheet:
  //   ROTACION A LA IZQUIERDA
endmodule

module SLT (
  input  [15:0] N1,
  input  [15:0] N2,
  output Bbit
);

  Comparator #(.width(16)) comparator_1 (.a(N1), .b(N2), .lt(Bbit));  // open: gt, eq
endmodule

module SGT (
  input  [15:0] N1,
  input  [15:0] N2,
  output Bbit
);

  Comparator #(.width(16)) comparator_1 (.a(N1), .b(N2), .gt(Bbit));  // open: eq, lt

  // Notes on the sheet:
  //   COMPARACION DEMAYOR QUE
endmodule

module EQ (
  input  [15:0] N1,
  input  [15:0] N2,
  output Branchbit
);

  wire comparator_1_eq, comparator_2_eq, comparator_3_eq, comparator_4_eq, comparator_5_eq, comparator_6_eq,
       comparator_7_eq, comparator_8_eq, comparator_9_eq, comparator_10_eq, comparator_11_eq,
       comparator_12_eq, comparator_13_eq, comparator_14_eq, comparator_15_eq, comparator_16_eq;

  Comparator #(.width(1)) comparator_1 (.a(N1[0]), .b(N2[0]), .eq(comparator_1_eq));  // open: gt, lt
  Comparator #(.width(1)) comparator_2 (.a(N1[1]), .b(N2[1]), .eq(comparator_2_eq));  // open: gt, lt
  Comparator #(.width(1)) comparator_3 (.a(N1[2]), .b(N2[2]), .eq(comparator_3_eq));  // open: gt, lt
  Comparator #(.width(1)) comparator_4 (.a(N1[3]), .b(N2[3]), .eq(comparator_4_eq));  // open: gt, lt
  Comparator #(.width(1)) comparator_5 (.a(N1[4]), .b(N2[4]), .eq(comparator_5_eq));  // open: gt, lt
  Comparator #(.width(1)) comparator_6 (.a(N1[5]), .b(N2[5]), .eq(comparator_6_eq));  // open: gt, lt
  Comparator #(.width(1)) comparator_7 (.a(N1[6]), .b(N2[6]), .eq(comparator_7_eq));  // open: gt, lt
  Comparator #(.width(1)) comparator_8 (.a(N1[7]), .b(N2[7]), .eq(comparator_8_eq));  // open: gt, lt
  Comparator #(.width(1)) comparator_9 (.a(N1[8]), .b(N2[8]), .eq(comparator_9_eq));  // open: gt, lt
  Comparator #(.width(1)) comparator_10 (.a(N1[9]), .b(N2[9]), .eq(comparator_10_eq));  // open: gt, lt
  Comparator #(.width(1)) comparator_11 (.a(N1[10]), .b(N2[10]), .eq(comparator_11_eq));  // open: gt, lt
  Comparator #(.width(1)) comparator_12 (.a(N1[11]), .b(N2[11]), .eq(comparator_12_eq));  // open: gt, lt
  Comparator #(.width(1)) comparator_13 (.a(N1[12]), .b(N2[12]), .eq(comparator_13_eq));  // open: gt, lt
  Comparator #(.width(1)) comparator_14 (.a(N1[13]), .b(N2[13]), .eq(comparator_14_eq));  // open: gt, lt
  Comparator #(.width(1)) comparator_15 (.a(N1[14]), .b(N2[14]), .eq(comparator_15_eq));  // open: gt, lt
  Comparator #(.width(1)) comparator_16 (.a(N1[15]), .b(N2[15]), .eq(comparator_16_eq));  // open: gt, lt
  and and_1 (Branchbit, comparator_1_eq, comparator_2_eq, comparator_3_eq, comparator_4_eq, comparator_5_eq, comparator_6_eq, comparator_7_eq, comparator_8_eq, comparator_9_eq, comparator_10_eq, comparator_11_eq, comparator_12_eq, comparator_13_eq, comparator_14_eq, comparator_15_eq, comparator_16_eq);
endmodule

module ALU (
  input  [3:0] NEM,
  input  [3:0] RD,
  input  [15:0] RS2,
  input  [15:0] RS1,
  output [15:0] Result,
  output Bbit
);

  wire demultiplexer_1_out0, demultiplexer_1_out1, demultiplexer_1_out2, demultiplexer_1_out3,
       demultiplexer_1_out4, demultiplexer_1_out5, demultiplexer_1_out6, demultiplexer_1_out7,
       eq_1_branchbit, multiplexer_7_out, multiplexer_8_out, not_1_out, sgt_1_bbit, slt_1_bbit;
  wire [15:0] add_1_result, and_1_re, divider_1_out, divider_1_rem, multiplexer_1_out, multiplexer_2_out,
       multiplexer_3_out, multiplexer_4_out, multiplexer_5_out, multiplexer_6_out, multiplier_1_out, or_1_re,
       rl_1_result, rr_1_result, sl_1_result, sr_1_result, sub_1_out_3, xor_1_resp;

  ADD add_1 (.B(RS2), .A(RS1), .Result(add_1_result));  // open: out_4
  Multiplexer #(.width(16), .enable("false")) multiplexer_1 (
    .in0(add_1_result), .in1(multiplier_1_out), .out(multiplexer_1_out), .sel(RD[0]));
  Multiplier #(.width(16)) multiplier_1 (.a(RS2), .b(RS1), .out(multiplier_1_out));  // open: cin, cout
  SUB sub_1 (.S(RS2), .M(RS1), .out_3(sub_1_out_3));  // open: Borrow
  Multiplexer #(.width(16), .enable("false")) multiplexer_2 (
    .in0(sub_1_out_3), .in1(divider_1_out), .out(multiplexer_2_out), .sel(RD[0]));
  Divider #(.width(16)) divider_1 (.a(RS1), .b(RS2), .out(divider_1_out), .rem(divider_1_rem));  // open: upper
  AND and_1 (.R1(RS1), .R2(RS2), .Re(and_1_re));
  Multiplexer #(.width(16), .enable("false")) multiplexer_3 (
    .in0(and_1_re), .in1(divider_1_rem), .out(multiplexer_3_out), .sel(RD[0]));
  OR or_1 (.R1(RS1), .R2(RS2), .Re(or_1_re));
  Multiplexer #(.width(16), .enable("false")) multiplexer_4 (
    .in0(or_1_re), .in1(xor_1_resp), .out(multiplexer_4_out), .sel(RD[0]));
  XOR xor_1 (.in_1(RS1), .in_2(RS2), .Resp(xor_1_resp));
  SR sr_1 (.N1(RS1), .Result(sr_1_result));  // open: Overflow
  Multiplexer #(.width(16), .enable("false")) multiplexer_5 (
    .in0(sr_1_result), .in1(rr_1_result), .out(multiplexer_5_out), .sel(RD[0]));
  RR rr_1 (.N1(RS1), .Result(rr_1_result));  // open: Overflow
  SL sl_1 (.N1(RS1), .Result(sl_1_result));  // open: Overflow
  Multiplexer #(.width(16), .enable("false")) multiplexer_6 (
    .in0(sl_1_result), .in1(rl_1_result), .out(multiplexer_6_out), .sel(RD[0]));
  RL rl_1 (.N1(RS1), .Result(rl_1_result));  // open: Overflow
  SLT slt_1 (.N1(RS1), .N2(RS2), .Bbit(slt_1_bbit));
  Multiplexer #(.enable("false")) multiplexer_7 (
    .in0(slt_1_bbit), .in1(sgt_1_bbit), .out(multiplexer_7_out), .sel(RD[0]));
  SGT sgt_1 (.N1(RS1), .N2(RS2), .Bbit(sgt_1_bbit));
  EQ eq_1 (.N1(RS1), .N2(RS2), .Branchbit(eq_1_branchbit));
  Multiplexer #(.enable("false")) multiplexer_8 (
    .in0(eq_1_branchbit), .in1(not_1_out), .out(multiplexer_8_out), .sel(RD[0]));
  not not_1 (not_1_out, eq_1_branchbit);
  assign Result = demultiplexer_1_out0 ? multiplexer_1_out : 16'bz;  // Controlled_Buffer controlled_buffer_1
  assign Result = demultiplexer_1_out1 ? multiplexer_2_out : 16'bz;  // Controlled_Buffer controlled_buffer_2
  assign Result = demultiplexer_1_out2 ? multiplexer_3_out : 16'bz;  // Controlled_Buffer controlled_buffer_3
  assign Result = demultiplexer_1_out3 ? multiplexer_4_out : 16'bz;  // Controlled_Buffer controlled_buffer_4
  assign Result = demultiplexer_1_out4 ? multiplexer_5_out : 16'bz;  // Controlled_Buffer controlled_buffer_5
  assign Result = demultiplexer_1_out5 ? multiplexer_6_out : 16'bz;  // Controlled_Buffer controlled_buffer_6
  assign Bbit = demultiplexer_1_out6 ? multiplexer_7_out : 1'bz;  // Controlled_Buffer controlled_buffer_7
  assign Bbit = demultiplexer_1_out7 ? multiplexer_8_out : 1'bz;  // Controlled_Buffer controlled_buffer_8
  Demultiplexer #(.select(4), .enable("false")) demultiplexer_1 (
    .out0(demultiplexer_1_out0), .out1(demultiplexer_1_out1), .out2(demultiplexer_1_out2),
    .out3(demultiplexer_1_out3), .out4(demultiplexer_1_out4), .out5(demultiplexer_1_out5),
    .out6(demultiplexer_1_out6), .out7(demultiplexer_1_out7), .in(1'b1), .sel(NEM));  // open: out8, out9, out10, out11, out12, out13, out14, out15

  // Notes on the sheet:
  //   Datos del estudiante
  //   Abdiel Mendoza
  //   3-749-1302
  //   UNIDAD ARITMETICA Y LOGICA
  //   1LS-132
endmodule
