// Logisim project JMP.circ as structural Verilog: 2 circuits, main circuit JMP
module JMP (
  input  [3:0] NEM,
  input  [3:0] RF2,
  input  [3:0] RF1,
  input  [3:0] RD,
  input  Bbit,
  input  [15:0] RF1_2,
  input  [15:0] PC,
  output [15:0] Imm,
  output Jact,
  output [15:0] PCdata,
  output CLS
);

  wire and_1_out, demultiplexer_1_out12, demultiplexer_1_out13, demultiplexer_1_out14, demultiplexer_1_out15,
       jr_bbr_1_s;
  wire [15:0] multiplexer_1_out;

  JR_BBR jr_bbr_1 (.RD_2(RD[0]), .BB(Bbit), .NM(demultiplexer_1_out14), .S(jr_bbr_1_s), .RD(RD));
  Demultiplexer #(.select(4), .enable("false")) demultiplexer_1 (
    .out12(demultiplexer_1_out12), .out13(demultiplexer_1_out13), .out14(demultiplexer_1_out14),
    .out15(demultiplexer_1_out15), .in(1'b1), .sel(NEM));  // open: out0, out1, out2, out3, out4, out5, out6, out7, out8, out9, out10, out11
  assign Imm = demultiplexer_1_out12 ? {4'b0000, RD, RF1, RF2} : 16'bz;  // Controlled_Buffer controlled_buffer_1
  assign Jact = demultiplexer_1_out12 ? 1'b1 : 1'bz;  // Controlled_Buffer controlled_buffer_2
  assign Imm = and_1_out ? {4'b0000, RD, RF1, RF2} : 16'bz;  // Controlled_Buffer controlled_buffer_3
  assign Jact = and_1_out ? 1'b1 : 1'bz;  // Controlled_Buffer controlled_buffer_4
  and and_1 (and_1_out, demultiplexer_1_out13, Bbit);
  assign Jact = jr_bbr_1_s ? 1'b1 : 1'bz;  // Controlled_Buffer controlled_buffer_5
  assign Imm = jr_bbr_1_s ? RF1_2 : 16'bz;  // Controlled_Buffer controlled_buffer_6
  Multiplexer #(.width(16), .enable("false")) multiplexer_1 (
    .in0(PC), .out(multiplexer_1_out), .sel(RD[0]));  // open: in1
  assign PCdata = demultiplexer_1_out15 ? multiplexer_1_out : 16'bz;  // Controlled_Buffer controlled_buffer_7
  assign CLS = demultiplexer_1_out15 ? RD[0] : 1'bz;  // Controlled_Buffer controlled_buffer_8

  // Notes on the sheet:
  //   SALTOS DIRECTOS E INDIRECTOS
  //   Datos del estudiante
  //   Abdiel Mendoza
  //   3-749-1302
  //   1LS-132
endmodule

module JR_BBR (
  input  [3:0] RD,
  input  RD_2,
  input  BB,
  input  NM,
  output S
);

  wire and_1_out, comparator_1_eq, not_1_out, not_2_out, or_1_out;

  Comparator #(.width(4)) comparator_1 (.a(RD), .b(4'b0001), .eq(comparator_1_eq));  // open: gt, lt
  not not_1 (not_1_out, RD_2);
  or or_1 (or_1_out, not_1_out, BB);
  and and_1 (and_1_out, NM, or_1_out);
  not not_2 (not_2_out, comparator_1_eq);
  and and_2 (S, and_1_out, not_2_out);
endmodule
