// Logisim project JR-BBR.circ as structural Verilog: 1 circuit, main circuit JR.BBR
module JR_BBR (
  input  [3:0] RD,
  input  RD_2,
  input  BB,
  input  NM,
  output S
);

  wire and_1_out, comparator_1_eq, not_1_out, not_2_out, or_1_out;

  Comparator #(.width(4)) comparator_1 (.a(RD), .b(4'b0001), .eq(comparator_1_eq));  // open: gt, lt
  not not_1 (not_1_out, RD_2);
  or or_1 (or_1_out, not_1_out, BB);
  and and_1 (and_1_out, NM, or_1_out);
  not not_2 (not_2_out, comparator_1_eq);
  and and_2 (S, and_1_out, not_2_out);
endmodule
