// Logisim project KeyTTY.circ as structural Verilog: 1 circuit, main circuit TTY-KEY
// TT-KEY
module TTY_KEY (
  input  [15:0] Data_R,
  input  [15:0] R0,
  input  [6:0] Asciikey,
  input  Bbit,
  output [15:0] Data,
  output [6:0] Asciitty,
  output Bit_7,
  output Bit_8
);

  wire and_1_out;

  Multiplexer #(.width(16), .enable("false")) multiplexer_1 (
    .in0(Data_R), .in1({{7{1'b0}}, {2{Bbit}}, Asciikey}), .out(Data), .sel(and_1_out));
  and and_1 (and_1_out, ~Bbit, R0[8]);  // AND_Gate

  assign Asciitty = R0[6:0];
  assign Bit_7 = R0[7];
  assign Bit_8 = R0[8];

  // Notes on the sheet:
  //   Datos del estudiante
  //   Abdiel Mendoza
  //   3-749-1302
  //   1LS-132
endmodule
