// Logisim project MEM.circ as structural Verilog: 5 circuits, main circuit MEM
// MEN
module MEM (
  input  [3:0] NEM,
  input  [3:0] RF1,
  input  [3:0] RF2,
  input  [3:0] RD,
  input  [15:0] Direccion_RF1,
  input  [15:0] Guardar_RF2,
  input  [15:0] Redest_RD,
  output [15:0] Resultados,
  output [15:0] Address_RF1,
  output [15:0] Store_RF2,
  output actR
);

  wire demultiplexer_1_out8, demultiplexer_1_out9, demultiplexer_1_out10, demultiplexer_1_out11, sb_1_sb;
  wire [15:0] controlled_buffer_6_out, li_1_result, lui_1_result, multiplexer_1_out, multiplexer_2_out,
       swp_1_result, undriven;

  Multiplexer #(.width(16), .enable("false")) multiplexer_1 (
    .in0(Guardar_RF2), .in1(undriven), .out(multiplexer_1_out), .sel(sb_1_sb));
  SWP swp_1 (.Result(swp_1_result), .RN1(Direccion_RF1));
  assign Address_RF1 = sb_1_sb ? Direccion_RF1 : 16'bz;  // Controlled_Buffer controlled_buffer_1
  assign actR = sb_1_sb ? 1'b1 : 1'bz;  // Controlled_Buffer controlled_buffer_2
  assign Store_RF2 = sb_1_sb ? Guardar_RF2 : 16'bz;  // Controlled_Buffer controlled_buffer_3
  assign Resultados = demultiplexer_1_out8 ? multiplexer_1_out : 16'bz;  // Controlled_Buffer controlled_buffer_4
  assign Address_RF1 = demultiplexer_1_out9 ? Direccion_RF1 : 16'bz;  // Controlled_Buffer controlled_buffer_5
  assign controlled_buffer_6_out = demultiplexer_1_out9 ? Redest_RD : 16'bz;  // Controlled_Buffer controlled_buffer_6
  Demultiplexer #(.select(4), .enable("false")) demultiplexer_1 (
    .out8(demultiplexer_1_out8), .out9(demultiplexer_1_out9), .out10(demultiplexer_1_out10),
    .out11(demultiplexer_1_out11), .in(1'b1), .sel(NEM));  // open: out0, out1, out2, out3, out4, out5, out6, out7, out12, out13, out14, out15
  LI li_1 (.Rdc1(RF1), .Rdc2(RF2), .Result(li_1_result));
  assign Resultados = demultiplexer_1_out10 ? li_1_result : 16'bz;  // Controlled_Buffer controlled_buffer_7
  LUI lui_1 (.Rdc1(RF1), .Rdc2(RF2), .Result(lui_1_result), .Rlow(Guardar_RF2));
  assign Resultados = demultiplexer_1_out11 ? lui_1_result : 16'bz;  // Controlled_Buffer controlled_buffer_8
  assign Resultados = demultiplexer_1_out9 ? multiplexer_2_out : 16'bz;  // Controlled_Buffer controlled_buffer_9
  Multiplexer #(.width(16), .enable("false")) multiplexer_2 (
    .in0(controlled_buffer_6_out), .in1(swp_1_result), .out(multiplexer_2_out), .sel(RD[0]));
  SB sb_1 (.RD(RD[0]), .NM(demultiplexer_1_out8), .SB(sb_1_sb));
  assign actR = demultiplexer_1_out9 ? 1'b0 : 1'bz;  // Controlled_Buffer controlled_buffer_10

  // Notes on the sheet:
  //   ADMINISTRADOR DE MEMORIA
  //   Datos del estudiante
  //   Abdiel Mendoza
  //   3-749-1302
  //   1LS-132
endmodule

module SB (
  input  RD,
  input  NM,
  output SB
);

  wire not_1_out;

  not not_1 (not_1_out, RD);
  and and_1 (SB, NM, not_1_out);
endmodule

module LUI (
  input  [3:0] Rdc1,
  input  [15:0] Rlow,
  input  [3:0] Rdc2,
  output [15:0] Result
);


  assign Result = {Rdc1, Rdc2, Rlow[7:0]};

  // Notes on the sheet:
  //   ALMACENAMIENTO PARTE ALTA
endmodule

module LI (
  input  [3:0] Rdc1,
  input  [3:0] Rdc2,
  output [15:0] Result
);


  assign Result = {{8{1'b0}}, Rdc1, Rdc2};
endmodule

module SWP (
  input  [15:0] RN1,
  output [15:0] Result
);


  assign Result = {RN1[7:0], RN1[15:8]};

  // Notes on the sheet:
  //   INTERCAMBIO BAJA <-> ALTA
endmodule
