// Logisim project MovLui.circ as structural Verilog: 1 circuit, main circuit MOV-LUI
module MOV_LUI (
  input  [3:0] RF2,
  input  [3:0] NEM,
  input  [3:0] RF1,
  input  [3:0] RD,
  output [3:0] out_5,
  output [3:0] out_6
);

  wire and_1_out, comparator_1_eq, comparator_2_eq;

  Comparator #(.width(4)) comparator_1 (.a(4'b1000), .b(NEM), .eq(comparator_1_eq));  // open: gt, lt
  and and_1 (and_1_out, comparator_1_eq, RD[0]);
  Multiplexer #(.width(4), .enable("false")) multiplexer_1 (.in0(RD), .in1(RF1), .out(out_5), .sel(and_1_out));
  Comparator #(.width(4)) comparator_2 (.a(4'b1011), .b(NEM), .eq(comparator_2_eq));  // open: gt, lt
  Multiplexer #(.width(4), .enable("false")) multiplexer_2 (.in0(RF2), .in1(RD), .out(out_6), .sel(comparator_2_eq));

  // Notes on the sheet:
  //   Datos del estudiante
  //   Abdiel Mendoza
  //   3-749-1302
  //   1LS-132
endmodule
