// Logisim project RST.circ as structural Verilog: 1 circuit, main circuit RST
module RST (
  input  [3:0] RD,
  input  [3:0] NEM,
  output RST
);

  wire comparator_1_eq, comparator_2_eq;

  Comparator #(.width(4)) comparator_1 (.a(NEM), .b(4'b1110), .eq(comparator_1_eq));  // open: gt, lt
  Comparator #(.width(4)) comparator_2 (.a(RD), .b(4'b0001), .eq(comparator_2_eq));  // open: gt, lt
  and and_1 (RST, comparator_2_eq, comparator_1_eq);

  // Notes on the sheet:
  //   Datos del estudiante
  //   Abdiel Mendoza
  //   3-749-1302
  //   1LS-132
endmodule
