// Logisim project Registro.circ as structural Verilog: 5 circuits, main circuit REG´S
// REG
module REG_S (
  input  [15:0] DataR,
  input  Bbit,
  input  [6:0] ASCII,
  input  [3:0] RF1,
  input  [3:0] RF2,
  input  [3:0] NEM,
  input  CLOCK,
  input  [3:0] RD,
  output [15:0] Rsrc2,
  output B8,
  output B7,
  output [6:0] Salida,
  output [15:0] Rsrc1
);

  wire demultiplexer_1_out0, demultiplexer_1_out1, demultiplexer_1_out2, demultiplexer_1_out3,
       demultiplexer_1_out4, demultiplexer_1_out5, demultiplexer_1_out6, demultiplexer_1_out7,
       demultiplexer_1_out8, demultiplexer_1_out9, demultiplexer_1_out10, demultiplexer_1_out11,
       demultiplexer_1_out12, demultiplexer_1_out13, demultiplexer_1_out14, demultiplexer_1_out15, rst_1_rst;
  wire [3:0] mov_lui_1_out_5, mov_lui_1_out_6, R0_2_out_2, R0_2_out_3, R0_2_out_4, R0_2_out_5, R0_2_out_6,
       R1_2_out_2, R1_2_out_3, R1_2_out_4, R1_2_out_5, R1_2_out_6, R2_2_out_2, R2_2_out_3, R2_2_out_4,
       R2_2_out_5, R2_2_out_6, R3_2_out_2, R3_2_out_3, R3_2_out_4, R3_2_out_5, R3_2_out_6, R4_2_out_2,
       R4_2_out_3, R4_2_out_4, R4_2_out_5, R4_2_out_6, R5_2_out_2, R5_2_out_3, R5_2_out_4, R5_2_out_5,
       R5_2_out_6, R6_2_out_2, R6_2_out_3, R6_2_out_4, R6_2_out_5, R6_2_out_6, R7_2_out_2, R7_2_out_3,
       R7_2_out_4, R7_2_out_5, R7_2_out_6, R8_2_out_2, R8_2_out_3, R8_2_out_4, R8_2_out_5, R8_2_out_6,
       R9_2_out_2, R9_2_out_3, R9_2_out_4, R9_2_out_5, R9_2_out_6, R10_2_out_2, R10_2_out_3, R10_2_out_4,
       R10_2_out_5, R10_2_out_6, R11_2_out_2, R11_2_out_3, R11_2_out_4, R11_2_out_5, R11_2_out_6,
       R12_2_out_2, R12_2_out_3, R12_2_out_4, R12_2_out_5, R12_2_out_6, R13_2_out_2, R13_2_out_3,
       R13_2_out_4, R13_2_out_5, R13_2_out_6, R14_2_out_2, R14_2_out_3, R14_2_out_4, R14_2_out_5,
       R14_2_out_6, R15_2_out_2, R15_2_out_3, R15_2_out_4, R15_2_out_5, R15_2_out_6;
  wire [15:0] R0_q, R1_q, R2_q, R3_q, R4_q, R5_q, R6_q, R7_q, R8_q, R9_q, R10_q, R11_q, R12_q, R13_q, R14_q,
       R15_q, tty_key_1_data;

  Demultiplexer #(.select(4), .enable("false")) demultiplexer_1 (
    .out0(demultiplexer_1_out0), .out1(demultiplexer_1_out1), .out2(demultiplexer_1_out2),
    .out3(demultiplexer_1_out3), .out4(demultiplexer_1_out4), .out5(demultiplexer_1_out5),
    .out6(demultiplexer_1_out6), .out7(demultiplexer_1_out7), .out8(demultiplexer_1_out8),
    .out9(demultiplexer_1_out9), .out10(demultiplexer_1_out10), .out11(demultiplexer_1_out11),
    .out12(demultiplexer_1_out12), .out13(demultiplexer_1_out13), .out14(demultiplexer_1_out14),
    .out15(demultiplexer_1_out15), .in(1'b1), .sel(mov_lui_1_out_5));
  TTY_KEY tty_key_1 (
    .Asciitty(Salida), .Data_R(DataR), .R0(R0_q), .Data(tty_key_1_data), .Bit_7(B7), .Asciikey(ASCII),
    .Bbit(Bbit), .Bit_8(B8));
  MOV_LUI mov_lui_1 (.RD(RD), .NEM(NEM), .RF1(RF1), .RF2(RF2), .out_5(mov_lui_1_out_5), .out_6(mov_lui_1_out_6));
  RST rst_1 (.RD(RD), .RST(rst_1_rst), .NEM(NEM));
  Register #(.width(16)) R0 (.D(tty_key_1_data), .en(demultiplexer_1_out0), .Q(R0_q), .clk(CLOCK), .clr(rst_1_rst));
  Register #(.width(16)) R2 (.D(DataR), .en(demultiplexer_1_out2), .Q(R2_q), .clk(CLOCK), .clr(rst_1_rst));
  Register #(.width(16)) R4 (.D(DataR), .en(demultiplexer_1_out4), .Q(R4_q), .clk(CLOCK), .clr(rst_1_rst));
  Register #(.width(16)) R6 (.D(DataR), .en(demultiplexer_1_out6), .Q(R6_q), .clk(CLOCK), .clr(rst_1_rst));
  Register #(.width(16)) R8 (.D(DataR), .en(demultiplexer_1_out8), .Q(R8_q), .clk(CLOCK), .clr(rst_1_rst));
  Register #(.width(16)) R10 (.D(DataR), .en(demultiplexer_1_out10), .Q(R10_q), .clk(CLOCK), .clr(rst_1_rst));
  Register #(.width(16)) R12 (.D(DataR), .en(demultiplexer_1_out12), .Q(R12_q), .clk(CLOCK), .clr(rst_1_rst));
  Register #(.width(16)) R14 (.D(DataR), .en(demultiplexer_1_out14), .Q(R14_q), .clk(CLOCK), .clr(rst_1_rst));
  Register #(.width(16)) R1 (.D(DataR), .en(demultiplexer_1_out1), .Q(R1_q), .clk(CLOCK), .clr(rst_1_rst));
  Register #(.width(16)) R3 (.D(DataR), .en(demultiplexer_1_out3), .Q(R3_q), .clk(CLOCK), .clr(rst_1_rst));
  Register #(.width(16)) R5 (.D(DataR), .en(demultiplexer_1_out5), .Q(R5_q), .clk(CLOCK), .clr(rst_1_rst));
  Register #(.width(16)) R7 (.D(DataR), .en(demultiplexer_1_out7), .Q(R7_q), .clk(CLOCK), .clr(rst_1_rst));
  Register #(.width(16)) R9 (.D(DataR), .en(demultiplexer_1_out9), .Q(R9_q), .clk(CLOCK), .clr(rst_1_rst));
  Register #(.width(16)) R11 (.D(DataR), .en(demultiplexer_1_out11), .Q(R11_q), .clk(CLOCK), .clr(rst_1_rst));
  Register #(.width(16)) R13 (.D(DataR), .en(demultiplexer_1_out13), .Q(R13_q), .clk(CLOCK), .clr(rst_1_rst));
  Register #(.width(16)) R15 (.D(DataR), .en(demultiplexer_1_out15), .Q(R15_q), .clk(CLOCK), .clr(rst_1_rst));
  Hex_Digit_Display hex_digit_display_1 (.value(R0_2_out_2));  // open: dp
  Binario_a_decimal_16_bits R0_2 (
    .in_1(R0_q), .out_2(R0_2_out_2), .out_3(R0_2_out_3), .out_4(R0_2_out_4), .out_5(R0_2_out_5),
    .out_6(R0_2_out_6));
  Hex_Digit_Display hex_digit_display_2 (.value(R3_2_out_2));  // open: dp
  Binario_a_decimal_16_bits R3_2 (
    .in_1(R3_q), .out_2(R3_2_out_2), .out_3(R3_2_out_3), .out_4(R3_2_out_4), .out_5(R3_2_out_5),
    .out_6(R3_2_out_6));
  Hex_Digit_Display hex_digit_display_3 (.value(R10_2_out_2));  // open: dp
  Binario_a_decimal_16_bits R10_2 (
    .in_1(R10_q), .out_2(R10_2_out_2), .out_3(R10_2_out_3), .out_4(R10_2_out_4), .out_5(R10_2_out_5),
    .out_6(R10_2_out_6));
  Hex_Digit_Display hex_digit_display_4 (.value(R13_2_out_2));  // open: dp
  Binario_a_decimal_16_bits R13_2 (
    .in_1(R13_q), .out_2(R13_2_out_2), .out_3(R13_2_out_3), .out_4(R13_2_out_4), .out_5(R13_2_out_5),
    .out_6(R13_2_out_6));
  Hex_Digit_Display hex_digit_display_5 (.value(R0_2_out_3));  // open: dp
  Hex_Digit_Display hex_digit_display_6 (.value(R0_2_out_4));  // open: dp
  Hex_Digit_Display hex_digit_display_7 (.value(R3_2_out_3));  // open: dp
  Hex_Digit_Display hex_digit_display_8 (.value(R3_2_out_4));  // open: dp
  Multiplexer #(.select(4), .width(16), .enable("false")) multiplexer_1 (
    .in0(R0_q), .in1(R1_q), .in2(R2_q), .in3(R3_q), .in4(R4_q), .in5(R5_q), .in6(R6_q), .in7(R7_q),
    .in8(R8_q), .in9(R9_q), .in10(R10_q), .in11(R11_q), .in12(R12_q), .in13(R13_q), .in14(R14_q),
    .in15(R15_q), .out(Rsrc2), .sel(mov_lui_1_out_6));
  Multiplexer #(.select(4), .width(16), .enable("false")) multiplexer_2 (
    .in0(R0_q), .in1(R1_q), .in2(R2_q), .in3(R3_q), .in4(R4_q), .in5(R5_q), .in6(R6_q), .in7(R7_q),
    .in8(R8_q), .in9(R9_q), .in10(R10_q), .in11(R11_q), .in12(R12_q), .in13(R13_q), .in14(R14_q),
    .in15(R15_q), .out(Rsrc1), .sel(RF1));
  Hex_Digit_Display hex_digit_display_9 (.value(R10_2_out_4));  // open: dp
  Hex_Digit_Display hex_digit_display_10 (.value(R10_2_out_3));  // open: dp
  Hex_Digit_Display hex_digit_display_11 (.value(R13_2_out_3));  // open: dp
  Hex_Digit_Display hex_digit_display_12 (.value(R13_2_out_4));  // open: dp
  Hex_Digit_Display hex_digit_display_13 (.value(R0_2_out_5));  // open: dp
  Hex_Digit_Display hex_digit_display_14 (.value(R0_2_out_6));  // open: dp
  Hex_Digit_Display hex_digit_display_15 (.value(R3_2_out_5));  // open: dp
  Hex_Digit_Display hex_digit_display_16 (.value(R3_2_out_6));  // open: dp
  Hex_Digit_Display hex_digit_display_17 (.value(R10_2_out_5));  // open: dp
  Hex_Digit_Display hex_digit_display_18 (.value(R10_2_out_6));  // open: dp
  Hex_Digit_Display hex_digit_display_19 (.value(R13_2_out_6));  // open: dp
  Hex_Digit_Display hex_digit_display_20 (.value(R13_2_out_5));  // open: dp
  Hex_Digit_Display hex_digit_display_21 (.value(R1_2_out_2));  // open: dp
  Hex_Digit_Display hex_digit_display_22 (.value(R1_2_out_3));  // open: dp
  Binario_a_decimal_16_bits R1_2 (
    .in_1(R1_q), .out_2(R1_2_out_2), .out_3(R1_2_out_3), .out_4(R1_2_out_4), .out_5(R1_2_out_5),
    .out_6(R1_2_out_6));
  Hex_Digit_Display hex_digit_display_23 (.value(R4_2_out_2));  // open: dp
  Hex_Digit_Display hex_digit_display_24 (.value(R4_2_out_3));  // open: dp
  Binario_a_decimal_16_bits R4_2 (
    .in_1(R4_q), .out_2(R4_2_out_2), .out_3(R4_2_out_3), .out_4(R4_2_out_4), .out_5(R4_2_out_5),
    .out_6(R4_2_out_6));
  Hex_Digit_Display hex_digit_display_25 (.value(R6_2_out_3));  // open: dp
  Hex_Digit_Display hex_digit_display_26 (.value(R6_2_out_2));  // open: dp
  Binario_a_decimal_16_bits R6_2 (
    .in_1(R6_q), .out_2(R6_2_out_2), .out_3(R6_2_out_3), .out_4(R6_2_out_4), .out_5(R6_2_out_5),
    .out_6(R6_2_out_6));
  Hex_Digit_Display hex_digit_display_27 (.value(R8_2_out_2));  // open: dp
  Hex_Digit_Display hex_digit_display_28 (.value(R8_2_out_3));  // open: dp
  Binario_a_decimal_16_bits R8_2 (
    .in_1(R8_q), .out_2(R8_2_out_2), .out_3(R8_2_out_3), .out_4(R8_2_out_4), .out_5(R8_2_out_5),
    .out_6(R8_2_out_6));
  Hex_Digit_Display hex_digit_display_29 (.value(R11_2_out_3));  // open: dp
  Hex_Digit_Display hex_digit_display_30 (.value(R11_2_out_2));  // open: dp
  Binario_a_decimal_16_bits R11_2 (
    .in_1(R11_q), .out_2(R11_2_out_2), .out_3(R11_2_out_3), .out_4(R11_2_out_4), .out_5(R11_2_out_5),
    .out_6(R11_2_out_6));
  Hex_Digit_Display hex_digit_display_31 (.value(R14_2_out_2));  // open: dp
  Hex_Digit_Display hex_digit_display_32 (.value(R14_2_out_3));  // open: dp
  Binario_a_decimal_16_bits R14_2 (
    .in_1(R14_q), .out_2(R14_2_out_2), .out_3(R14_2_out_3), .out_4(R14_2_out_4), .out_5(R14_2_out_5),
    .out_6(R14_2_out_6));
  Hex_Digit_Display hex_digit_display_33 (.value(R1_2_out_4));  // open: dp
  Hex_Digit_Display hex_digit_display_34 (.value(R1_2_out_5));  // open: dp
  Hex_Digit_Display hex_digit_display_35 (.value(R4_2_out_4));  // open: dp
  Hex_Digit_Display hex_digit_display_36 (.value(R4_2_out_5));  // open: dp
  Hex_Digit_Display hex_digit_display_37 (.value(R6_2_out_5));  // open: dp
  Hex_Digit_Display hex_digit_display_38 (.value(R6_2_out_4));  // open: dp
  Hex_Digit_Display hex_digit_display_39 (.value(R8_2_out_4));  // open: dp
  Hex_Digit_Display hex_digit_display_40 (.value(R8_2_out_5));  // open: dp
  Hex_Digit_Display hex_digit_display_41 (.value(R11_2_out_4));  // open: dp
  Hex_Digit_Display hex_digit_display_42 (.value(R11_2_out_5));  // open: dp
  Hex_Digit_Display hex_digit_display_43 (.value(R14_2_out_4));  // open: dp
  Hex_Digit_Display hex_digit_display_44 (.value(R14_2_out_5));  // open: dp
  Hex_Digit_Display hex_digit_display_45 (.value(R2_2_out_2));  // open: dp
  Hex_Digit_Display hex_digit_display_46 (.value(R1_2_out_6));  // open: dp
  Binario_a_decimal_16_bits R2_2 (
    .in_1(R2_q), .out_2(R2_2_out_2), .out_3(R2_2_out_3), .out_4(R2_2_out_4), .out_5(R2_2_out_5),
    .out_6(R2_2_out_6));
  Hex_Digit_Display hex_digit_display_47 (.value(R5_2_out_2));  // open: dp
  Hex_Digit_Display hex_digit_display_48 (.value(R4_2_out_6));  // open: dp
  Binario_a_decimal_16_bits R5_2 (
    .in_1(R5_q), .out_2(R5_2_out_2), .out_3(R5_2_out_3), .out_4(R5_2_out_4), .out_5(R5_2_out_5),
    .out_6(R5_2_out_6));
  Hex_Digit_Display hex_digit_display_49 (.value(R6_2_out_6));  // open: dp
  Hex_Digit_Display hex_digit_display_50 (.value(R7_2_out_2));  // open: dp
  Binario_a_decimal_16_bits R7_2 (
    .in_1(R7_q), .out_2(R7_2_out_2), .out_3(R7_2_out_3), .out_4(R7_2_out_4), .out_5(R7_2_out_5),
    .out_6(R7_2_out_6));
  Hex_Digit_Display hex_digit_display_51 (.value(R8_2_out_6));  // open: dp
  Hex_Digit_Display hex_digit_display_52 (.value(R9_2_out_2));  // open: dp
  Binario_a_decimal_16_bits R9_2 (
    .in_1(R9_q), .out_2(R9_2_out_2), .out_3(R9_2_out_3), .out_4(R9_2_out_4), .out_5(R9_2_out_5),
    .out_6(R9_2_out_6));
  Hex_Digit_Display hex_digit_display_53 (.value(R11_2_out_6));  // open: dp
  Hex_Digit_Display hex_digit_display_54 (.value(R12_2_out_2));  // open: dp
  Binario_a_decimal_16_bits R12_2 (
    .in_1(R12_q), .out_2(R12_2_out_2), .out_3(R12_2_out_3), .out_4(R12_2_out_4), .out_5(R12_2_out_5),
    .out_6(R12_2_out_6));
  Hex_Digit_Display hex_digit_display_55 (.value(R15_2_out_2));  // open: dp
  Hex_Digit_Display hex_digit_display_56 (.value(R14_2_out_6));  // open: dp
  Binario_a_decimal_16_bits R15_2 (
    .in_1(R15_q), .out_2(R15_2_out_2), .out_3(R15_2_out_3), .out_4(R15_2_out_4), .out_5(R15_2_out_5),
    .out_6(R15_2_out_6));
  Hex_Digit_Display hex_digit_display_57 (.value(R2_2_out_4));  // open: dp
  Hex_Digit_Display hex_digit_display_58 (.value(R2_2_out_3));  // open: dp
  Hex_Digit_Display hex_digit_display_59 (.value(R5_2_out_4));  // open: dp
  Hex_Digit_Display hex_digit_display_60 (.value(R5_2_out_3));  // open: dp
  Hex_Digit_Display hex_digit_display_61 (.value(R7_2_out_3));  // open: dp
  Hex_Digit_Display hex_digit_display_62 (.value(R7_2_out_4));  // open: dp
  Hex_Digit_Display hex_digit_display_63 (.value(R9_2_out_4));  // open: dp
  Hex_Digit_Display hex_digit_display_64 (.value(R9_2_out_3));  // open: dp
  Hex_Digit_Display hex_digit_display_65 (.value(R12_2_out_3));  // open: dp
  Hex_Digit_Display hex_digit_display_66 (.value(R12_2_out_4));  // open: dp
  Hex_Digit_Display hex_digit_display_67 (.value(R15_2_out_4));  // open: dp
  Hex_Digit_Display hex_digit_display_68 (.value(R15_2_out_3));  // open: dp
  Hex_Digit_Display hex_digit_display_69 (.value(R2_2_out_6));  // open: dp
  Hex_Digit_Display hex_digit_display_70 (.value(R2_2_out_5));  // open: dp
  Hex_Digit_Display hex_digit_display_71 (.value(R5_2_out_6));  // open: dp
  Hex_Digit_Display hex_digit_display_72 (.value(R5_2_out_5));  // open: dp
  Hex_Digit_Display hex_digit_display_73 (.value(R7_2_out_5));  // open: dp
  Hex_Digit_Display hex_digit_display_74 (.value(R7_2_out_6));  // open: dp
  Hex_Digit_Display hex_digit_display_75 (.value(R9_2_out_6));  // open: dp
  Hex_Digit_Display hex_digit_display_76 (.value(R9_2_out_5));  // open: dp
  Hex_Digit_Display hex_digit_display_77 (.value(R12_2_out_6));  // open: dp
  Hex_Digit_Display hex_digit_display_78 (.value(R12_2_out_5));  // open: dp
  Hex_Digit_Display hex_digit_display_79 (.value(R15_2_out_5));  // open: dp
  Hex_Digit_Display hex_digit_display_80 (.value(R15_2_out_6));  // open: dp

  // Notes on the sheet:
  //   REGISTROS
  //   Datos del estudiante
  //   Abdiel Mendoza
  //   3-749-1302
  //   1LS-132
endmodule

// TT-KEY
module TTY_KEY (
  input  [15:0] Data_R,
  input  [15:0] R0,
  input  [6:0] Asciikey,
  input  Bbit,
  output [15:0] Data,
  output [6:0] Asciitty,
  output Bit_7,
  output Bit_8
);

  wire and_1_out;

  Multiplexer #(.width(16), .enable("false")) multiplexer_1 (
    .in0(Data_R), .in1({{7{1'b0}}, {2{Bbit}}, Asciikey}), .out(Data), .sel(and_1_out));
  and and_1 (and_1_out, ~Bbit, R0[8]);  // AND_Gate

  assign Asciitty = R0[6:0];
  assign Bit_7 = R0[7];
  assign Bit_8 = R0[8];

  // Notes on the sheet:
  //   Datos del estudiante
  //   Abdiel Mendoza
  //   3-749-1302
  //   1LS-132
endmodule

module RST (
  input  [3:0] RD,
  input  [3:0] NEM,
  output RST
);

  wire comparator_1_eq, comparator_2_eq;

  Comparator #(.width(4)) comparator_1 (.a(NEM), .b(4'b1110), .eq(comparator_1_eq));  // open: gt, lt
  Comparator #(.width(4)) comparator_2 (.a(RD), .b(4'b0001), .eq(comparator_2_eq));  // open: gt, lt
  and and_1 (RST, comparator_2_eq, comparator_1_eq);

  // Notes on the sheet:
  //   Datos del estudiante
  //   Abdiel Mendoza
  //   3-749-1302
  //   1LS-132
endmodule

module MOV_LUI (
  input  [3:0] RF2,
  input  [3:0] NEM,
  input  [3:0] RF1,
  input  [3:0] RD,
  output [3:0] out_5,
  output [3:0] out_6
);

  wire and_1_out, comparator_1_eq, comparator_2_eq;

  Comparator #(.width(4)) comparator_1 (.a(4'b1000), .b(NEM), .eq(comparator_1_eq));  // open: gt, lt
  and and_1 (and_1_out, comparator_1_eq, RD[0]);
  Multiplexer #(.width(4), .enable("false")) multiplexer_1 (.in0(RD), .in1(RF1), .out(out_5), .sel(and_1_out));
  Comparator #(.width(4)) comparator_2 (.a(4'b1011), .b(NEM), .eq(comparator_2_eq));  // open: gt, lt
  Multiplexer #(.width(4), .enable("false")) multiplexer_2 (.in0(RF2), .in1(RD), .out(out_6), .sel(comparator_2_eq));

  // Notes on the sheet:
  //   Datos del estudiante
  //   Abdiel Mendoza
  //   3-749-1302
  //   1LS-132
endmodule

module Binario_a_decimal_16_bits (
  input  [15:0] in_1,
  output [3:0] out_2,
  output [3:0] out_3,
  output [3:0] out_4,
  output [3:0] out_5,
  output [3:0] out_6
);

  wire [15:0] divider_1_out, divider_1_rem, divider_2_out, divider_2_rem, divider_3_out, divider_3_rem,
       divider_4_out, divider_4_rem;

  Divider #(.width(16)) divider_1 (.a(in_1), .b(16'h2710), .out(divider_1_out), .rem(divider_1_rem));  // open: upper
  Divider #(.width(16)) divider_2 (
    .a(divider_1_rem), .b(16'h3e8), .out(divider_2_out), .rem(divider_2_rem));  // open: upper
  Divider #(.width(16)) divider_3 (
    .a(divider_2_rem), .b(16'h64), .out(divider_3_out), .rem(divider_3_rem));  // open: upper
  Divider #(.width(16)) divider_4 (
    .a(divider_3_rem), .b(16'ha), .out(divider_4_out), .rem(divider_4_rem));  // open: upper
  Bit_Extender #(.in_width(16), .out_width(4)) bit_extender_1 (.in(divider_1_out), .out(out_2));
  Bit_Extender #(.in_width(16), .out_width(4)) bit_extender_2 (.in(divider_2_out), .out(out_3));
  Bit_Extender #(.in_width(16), .out_width(4)) bit_extender_3 (.in(divider_3_out), .out(out_4));
  Bit_Extender #(.in_width(16), .out_width(4)) bit_extender_4 (.in(divider_4_out), .out(out_5));
  Bit_Extender #(.in_width(16), .out_width(4)) bit_extender_5 (.in(divider_4_rem), .out(out_6));
endmodule
