// Logisim project SB.circ as structural Verilog: 1 circuit, main circuit SB
module SB (
  input  RD,
  input  NM,
  output SB
);

  wire not_1_out;

  not not_1 (not_1_out, RD);
  and and_1 (SB, NM, not_1_out);
endmodule
