// Logisim project SGT.circ as structural Verilog: 1 circuit, main circuit sgt
module sgt (
  input  [15:0] N1,
  input  [15:0] N2,
  output Bbit
);

  Comparator #(.width(16)) comparator_1 (.a(N1), .b(N2), .gt(Bbit));  // open: eq, lt

  // Notes on the sheet:
  //   COMPARACION DEMAYOR QUE
endmodule
